// Logisim project cpu24.circ as structural Verilog: 21 circuits, main circuit ◇单周期MIPS
module \单周期MIPS  (
  input  IR1,
  input  IR2,
  input  IR3,
  output RegWrite,
  output MemWrite,
  output [31:0] PC,
  output [31:0] IR,
  output [31:0] RDin,
  output [31:0] MDin,
  output [31:0] LedData,
  output [31:0] v0,
  output [31:0] a0,
  output [31:0] PC_2
);

  wire AluSrcB, and_1_out, and_2_out, and_3_out, Beq, Bne, CLK, clock_2_out, comparator_1_eq,
       comparator_1_lt, comparator_2_eq, d_ff_1_q, equal, Go, Halt, IR1_t, IR2_t, IR3_t, IRA, IRB, IRC, JAL,
       JMP, JR, MemToReg, multiplexer_4_out, nand_1_out, not_1_out, not_2_out, not_3_out, not_4_out, RegDst,
       SignedExt, Syscall, W1, W2, W3;
  wire [3:0] AluOP;
  wire [4:0] multiplexer_5_out, multiplexer_6_out, multiplexer_7_out, multiplexer_8_out;
  wire [12:0] CNT_num;
  wire [15:0] \总周期数 ;
  wire [31:0] adder_1_out, adder_2_out, bit_extender_1_out, bit_extender_2_out, mips_alu_1_result,
       multiplexer_1_out, multiplexer_2_out, multiplexer_3_out, multiplexer_9_out, multiplexer_10_out,
       multiplexer_12_out, ram_1_data, shifter_1_out;

  Clock #(.highDuration(1), .lowDuration(1)) clock_1 ();  // open: out
  Button _1 (.out(IRA));
  Button _2 (.out(IRB));
  Button _3 (.out(IRC));
  Button \u_继续运行  (.out(Go));
  LED #(.active("true")) led_1 (.in(W1));
  LED #(.active("true")) led_2 (.in(W2));
  LED #(.active("true")) led_3 (.in(W3));
  Hex_Digit_Display hex_digit_display_1 (.value(LedData[31:28]));  // open: dp
  D_Flip_Flop #(.trigger("high"), .Pre_Clr_Positions("LEGACY"), .NegatePresetClear("false"), .enable("true"), .NewFFLayout("false")) d_ff_1 (.Q(d_ff_1_q));  // open: clk, D, Qn, preset, en, reset
  // Probe on 13'hc
  Hex_Digit_Display hex_digit_display_2 (.value(LedData[27:24]));  // open: dp
  Hex_Digit_Display hex_digit_display_3 (.value(LedData[23:20]));  // open: dp
  Comparator #(.width(13), .mode("twosComplement")) comparator_1 (
    .a(CNT_num), .b(13'hc), .eq(comparator_1_eq), .lt(comparator_1_lt));  // open: gt
  Clock #(.highDuration(1), .lowDuration(1)) clock_2 (.out(clock_2_out));
  Hex_Digit_Display hex_digit_display_4 (.value(LedData[15:12]));  // open: dp
  Hex_Digit_Display hex_digit_display_5 (.value(LedData[19:16]));  // open: dp
  Counter #(.width(13), .max('h1fff), .ongoal("stay"), .trigger("rising"), .behavior("old")) counter_1 (
    .count(comparator_1_lt), .Q(CNT_num), .clk(clock_2_out));  // open: load, D, carry, clr, preset
  Hex_Digit_Display hex_digit_display_6 (.value(LedData[11:8]));  // open: dp
  Hex_Digit_Display hex_digit_display_7 (.value(LedData[7:4]));  // open: dp
  // Probe on \总周期数 
  nand nand_1 (nand_1_out, d_ff_1_q, comparator_1_eq);
  Hex_Digit_Display hex_digit_display_8 (.value(LedData[3:0]));  // open: dp
  assign CLK = nand_1_out ? clock_2_out : 1'bz;  // Controlled_Buffer controlled_buffer_1
  Pull_Resistor #(.pull(1)) pull_resistor_1 (.node(CLK));
  not not_1 (not_1_out, Halt);
  Multiplexer #(.select(1), .width(32), .disabled("Z"), .enable("false")) multiplexer_1 (
    .in0(multiplexer_3_out), .in1(multiplexer_2_out), .out(multiplexer_1_out), .sel(JMP));
  Counter #(.width(16), .max('hffff), .ongoal("wrap"), .trigger("rising"), .behavior("old")) counter_2 (
    .count(not_1_out), .Q(\总周期数 ), .clk(and_1_out));  // open: load, D, carry, clr, preset
  and and_1 (and_1_out, not_2_out, CLK);
  not not_2 (not_2_out, Halt);
  Register #(.width(32), .trigger("rising"), .Select("low")) u_PC (
    .D(multiplexer_1_out), .en(not_1_out), .Q(PC), .clk(CLK));  // open: clr
  Multiplexer #(.select(1), .width(32), .disabled("Z"), .enable("false")) multiplexer_2 (
    .in0({PC[31:28], IR[25:0], 2'b00}), .in1(v0), .out(multiplexer_2_out), .sel(JR));
  or or_1 (IR1_t, IR1, IRA);
  Adder #(.width(32)) adder_1 (.a(PC), .b(32'h4), .out(adder_1_out));  // open: cin, cout
  or or_2 (IR2_t, IR2, IRB);
  Comparator #(.width(32), .mode("twosComplement")) comparator_2 (
    .a(v0), .b(32'h32), .eq(comparator_2_eq));  // open: gt, lt
  Multiplexer #(.select(1), .width(32), .disabled("Z"), .enable("false")) multiplexer_3 (
    .in0(adder_1_out), .in1(adder_2_out), .out(multiplexer_3_out), .sel(multiplexer_4_out));
  not not_3 (not_3_out, comparator_2_eq);
  and and_2 (and_2_out, not_3_out, Syscall);
  and and_3 (and_3_out, Syscall, comparator_2_eq);
  ROM #(.addrWidth(10), .dataWidth(32), .Select("high")) rom_1 (.addr(PC[11:2]), .data(IR));
  Multiplexer #(.select(1), .width(1), .disabled("Z"), .enable("false")) multiplexer_4 (
    .in0(Bne), .in1(Beq), .out(multiplexer_4_out), .sel(equal));
  or or_3 (IR3_t, IR3, IRC);
  Register #(.width(32), .trigger("rising"), .Select("low")) register_1 (
    .D(a0), .en(and_2_out), .Q(LedData), .clk(CLK));  // open: clr
  Register #(.width(1), .trigger("rising"), .Select("low")) register_2 (
    .D(and_3_out), .en(and_3_out), .Q(Halt), .clk(CLK), .clr(Go));
  assign bit_extender_1_out = {{16{1'b0}}, IR[15:0]};  // Bit_Extender bit_extender_1
  assign bit_extender_2_out = {{16{IR[15]}}, IR[15:0]};  // Bit_Extender bit_extender_2
  Multiplexer #(.select(1), .width(5), .disabled("Z"), .enable("false")) multiplexer_5 (
    .in0(IR[25:21]), .in1(5'b00010), .out(multiplexer_5_out), .sel(Syscall));
  Multiplexer #(.select(1), .width(5), .disabled("Z"), .enable("false")) multiplexer_6 (
    .in0(IR[20:16]), .in1(IR[15:11]), .out(multiplexer_6_out), .sel(RegDst));
  Multiplexer #(.select(1), .width(5), .disabled("Z"), .enable("false")) multiplexer_7 (
    .in0(IR[20:16]), .in1(5'b00100), .out(multiplexer_7_out), .sel(Syscall));
  Multiplexer #(.select(1), .width(5), .disabled("Z"), .enable("false")) multiplexer_8 (
    .in0(multiplexer_6_out), .in1({5{1'b1}}), .out(multiplexer_8_out), .sel(JAL));
  Multiplexer #(.select(1), .width(32), .disabled("Z"), .enable("false")) multiplexer_9 (
    .in0(bit_extender_1_out), .in1(bit_extender_2_out), .out(multiplexer_9_out), .sel(SignedExt));
  MIPS_Regifile mips_regifile_1 (
    .Din(RDin), .Clk(CLK), .R1(v0), .R2(a0), .WE(RegWrite), .W_num(multiplexer_8_out),
    .R1_num(multiplexer_5_out), .R2_num(multiplexer_7_out));
  Shifter #(.width(32), .shift("ll")) shifter_1 (.in(bit_extender_2_out), .\dist (5'b00010), .out(shifter_1_out));
  Multiplexer #(.select(1), .width(32), .disabled("Z"), .enable("false")) multiplexer_10 (
    .in0(a0), .in1(multiplexer_9_out), .out(multiplexer_10_out), .sel(AluSrcB));
  Adder #(.width(32)) adder_2 (.a(shifter_1_out), .b(adder_1_out), .out(adder_2_out));  // open: cin, cout
  \单周期硬布线控制器  \u_单周期硬布线控制器_1  (
    .Func(IR[5:0]), .OP(IR[31:26]), .ALU_OP(AluOP), .MemToReg(MemToReg), .MemWrite(MemWrite),
    .ALU_SRC(AluSrcB), .RegWrite(RegWrite), .SysCALL(Syscall), .SignedExt(SignedExt), .RegDst(RegDst),
    .JR(JR), .JMP(JMP), .Beq(Beq), .JAL(JAL), .Bne(Bne));
  MIPS_ALU mips_alu_1 (
    .X(v0), .Y(multiplexer_10_out), .AluOP(AluOP), .Equal(equal), .Result(mips_alu_1_result), .shamt(IR[10:6]));  // open: Result_2
  Multiplexer #(.select(1), .width(32), .disabled("Z"), .enable("false")) multiplexer_11 (
    .in0(multiplexer_12_out), .in1(adder_1_out), .out(RDin), .sel(JAL));
  Multiplexer #(.select(1), .width(32), .disabled("Z"), .enable("false")) multiplexer_12 (
    .in0(mips_alu_1_result), .in1(ram_1_data), .out(multiplexer_12_out), .sel(MemToReg));
  not not_4 (not_4_out, Halt);
  RAM #(.addrWidth(10), .dataWidth(32), .bus("separate"), .Select("high")) ram_1 (
    .addr(mips_alu_1_result[11:2]), .din(a0), .data(ram_1_data), .str(MemWrite), .sel(not_4_out), .clk(CLK));  // open: ld, clr

  assign MDin = a0;
  assign PC_2 = {PC[31:28], IR[25:0], 2'b00};

  // Other names for the same wires on the sheet: OP[5:0] = IR[31:26]; Func[5:0] = IR[5:0];
  //   JAddr[31:2] = {PC[31:28], IR[25:0]}; shamt[4:0] = IR[10:6]; rd[4:0] = IR[15:11]; rt[4:0] = IR[20:16];
  //   rs_t[4:0] = IR[25:21]; PC_OUT[31:0] = PC; RS[31:0] = v0

  // Notes on the sheet:
  //   中断源
  //   中断等待指示
  //   总复位信号应将除ROM以外所有存储组件全部清零
  //   控制位
  //   暂停节拍，不能为0
  //   数码管输出
  //   可计数暂停的时钟源
  //   指令存储器
  //   指令字
  //   contents of rom_1 (hex, n*v repeats v):
  //   20110001 8000c05 20110001 20120002 20130003 8000c09 20110001 20120002 20130003 8000c0d 20110001
  //   20120002 20130003 8000c11 20110001 20120002 20130003 c000cb8 20100001 20110001 118fc0 112020
  //   20020022 c 118882 12200001 8000c15 112020 20020022 c 20110001 118880 112020 20020022 c 12200001
  //   8000c1f 20110001 118fc0 112020 20020022 c 1188c3 112020 20020022 c 118903 112020 20020022 c 118903
  //   112020 20020022 c 118903 112020 20020022 c 118903 112020 20020022 c 118903 112020 20020022 c 118903
  //   112020 20020022 c 118903 112020 20020022 c 20100001 109fc0 139fc3 8021 2012000c 24160003 26100001
  //   3210000f 20080008 20090001 139900 2709825 132020 20020022 c 1094022 1500fff9 22100001 2018000f
  //   2188024 108700 20080008 20090001 139902 2709825 132021 20020022 c 1094022 1500fff9 108702 2c9b022
  //   12c00001 8000c50 4020 1084027 84400 3508ffff 82021 20020022 c 2010ffff 20110000 ae300000 22100001
  //   22310004 ae300000 22100001 22310004 ae300000 22100001 22310004 ae300000 22100001 22310004 ae300000
  //   22100001 22310004 ae300000 22100001 22310004 ae300000 22100001 22310004 ae300000 22100001 22310004
  //   ae300000 22100001 22310004 ae300000 22100001 22310004 ae300000 22100001 22310004 ae300000 22100001
  //   22310004 ae300000 22100001 22310004 ae300000 22100001 22310004 ae300000 22100001 22310004 ae300000
  //   22100001 22310004 22100001 8020 2011003c 8e130000 8e340000 274402a 11000002 ae330000 ae140000
  //   2231fffc 1611fff8 102020 20020022 c 22100004 2011003c 1611fff2 20020032 c 20100000 22100001 102020
  //   20020022 c 22100002 102020 20020022 c 22100003 102020 20020022 c 22100004 102020 20020022 c 22100005
  //   102020 20020022 c 22100006 102020 20020022 c 22100007 102020 20020022 c 22100008 102020 20020022
  //   20020022 c 3e00008
  //   OP
  //   rs
  //   rt
  //   rd
  //   为方便自动评测，需要输出PC，IR，寄存器堆写如数据RDin
  //   RAM写使能MemWrite、RAM写入数据MDin等信号
  //   JMP
  //   JR
  //   OP
  //   Func
  //   Beq
  //   Bne
  //   MemToReg
  //   MemWrite
  //   AluOP
  //   AluSrcB
  //   RegWrite
  //   JAL
  //   RegDst
  //   Syscall
endmodule

// 单周期硬布线控制器
module \单周期硬布线控制器  (
  input  [5:0] OP,
  input  [5:0] Func,
  output [3:0] ALU_OP,
  output MemToReg,
  output MemWrite,
  output ALU_SRC,
  output RegWrite,
  output SysCALL,
  output SignedExt,
  output RegDst,
  output Beq,
  output Bne,
  output JR,
  output JMP,
  output JAL
);

  \运算控制器自动生成  \u_运算控制器自动生成_1  (
    .OP0(OP[0]), .OP1(OP[1]), .OP2(OP[2]), .OP3(OP[3]), .OP4(OP[4]), .OP5(OP[5]), .F0(Func[0]), .F1(Func[1]),
    .F2(Func[2]), .F3(Func[3]), .F4(Func[4]), .F5(Func[5]), .S0(ALU_OP[0]), .S1(ALU_OP[1]), .S2(ALU_OP[2]),
    .S3(ALU_OP[3]));
  \控制信号自动生成  \u_控制信号自动生成_1  (
    .OP0(OP[0]), .OP1(OP[1]), .OP2(OP[2]), .OP3(OP[3]), .OP4(OP[4]), .OP5(OP[5]), .F0(Func[0]), .F1(Func[1]),
    .F2(Func[2]), .F3(Func[3]), .F4(Func[4]), .F5(Func[5]), .MemToReg(MemToReg), .MemWrite(MemWrite),
    .ALU_SRC(ALU_SRC), .RegWrite(RegWrite), .SysCALL(SysCALL), .SignedExt(SignedExt), .RegDst(RegDst),
    .BEQ(Beq), .BNE(Bne), .JR(JR), .JUMP(JMP), .JAL(JAL));

  // Other names for the same wires on the sheet: OP_CODE[5:0] = OP

  // Notes on the sheet:
  //   运算器控制器，根据指令生成运算器功能选择信号
  //   控制信号生成，产生数据通路需要的其他控制信号
endmodule

// 运算器控制器
module \运算控制器自动生成  (
  input  OP0,
  input  OP1,
  input  OP2,
  input  OP3,
  input  OP4,
  input  OP5,
  input  F0,
  input  F1,
  input  F2,
  input  F3,
  input  F4,
  input  F5,
  output S0,
  output S1,
  output S2,
  output S3
);

  wire and_1_out, and_2_out, and_3_out, and_4_out, and_5_out, and_6_out, and_7_out, and_8_out, and_9_out,
       and_10_out, and_11_out, and_12_out, and_13_out, and_14_out, and_15_out, and_16_out, and_17_out,
       and_18_out, and_19_out, and_20_out, and_21_out, and_22_out, and_23_out, and_24_out, and_25_out,
       and_26_out, and_27_out, and_28_out, and_29_out, and_30_out, and_31_out, and_32_out, and_33_out,
       and_34_out, not_1_out, not_2_out, not_3_out, not_4_out, not_5_out, not_6_out, not_7_out, not_8_out,
       not_9_out, not_10_out, not_11_out, not_12_out, not_13_out, not_14_out, not_15_out, not_16_out,
       not_17_out, not_18_out, not_19_out, not_20_out, not_21_out, not_22_out, not_23_out, not_24_out,
       not_25_out, not_26_out, not_27_out, not_28_out, not_29_out, not_30_out, not_31_out, not_32_out,
       not_33_out, not_34_out, not_35_out, not_36_out, not_37_out, not_38_out, not_39_out, not_40_out,
       not_41_out, not_42_out, not_43_out, not_44_out, not_45_out, not_46_out, not_47_out, not_48_out,
       not_49_out, not_50_out, not_51_out, not_52_out, not_53_out, not_54_out, not_55_out, not_56_out,
       not_57_out, not_58_out, not_59_out, not_60_out, not_61_out, not_62_out, not_63_out, not_64_out,
       not_65_out, not_66_out, not_67_out, not_68_out, not_69_out, not_70_out, not_71_out, not_72_out,
       not_73_out, not_74_out, not_75_out, not_76_out, not_77_out, not_78_out, not_79_out, not_80_out,
       not_81_out, not_82_out, not_83_out, not_84_out, not_85_out, not_86_out, not_87_out, not_88_out,
       not_89_out, not_90_out, not_91_out, not_92_out, not_93_out, not_94_out, not_95_out, not_96_out,
       not_97_out, not_98_out, not_99_out, not_100_out, not_101_out, not_102_out, not_103_out, not_104_out,
       not_105_out, not_106_out, not_107_out, not_108_out, not_109_out, not_110_out, not_111_out,
       not_112_out, not_113_out, not_114_out, not_115_out, not_116_out, not_117_out, not_118_out,
       not_119_out, not_120_out, not_121_out, not_122_out, not_123_out, not_124_out, not_125_out,
       not_126_out, not_127_out, not_128_out, not_129_out, not_130_out, not_131_out, not_132_out,
       not_133_out, not_134_out, not_135_out, not_136_out, not_137_out, not_138_out, not_139_out,
       not_140_out, not_141_out, not_142_out, not_143_out, not_144_out, not_145_out, not_146_out,
       not_147_out, not_148_out, not_149_out, not_150_out, not_151_out, not_152_out, not_153_out,
       not_154_out, not_155_out, not_156_out, not_157_out, not_158_out, not_159_out, not_160_out,
       not_161_out, not_162_out, not_163_out, not_164_out, not_165_out, not_166_out, not_167_out,
       not_168_out, not_169_out, not_170_out, not_171_out, not_172_out, not_173_out, not_174_out,
       not_175_out, not_176_out, not_177_out, not_178_out, not_179_out, not_180_out, not_181_out,
       not_182_out, not_183_out, not_184_out, not_185_out, not_186_out, not_187_out, not_188_out,
       not_189_out, not_190_out, not_191_out, not_192_out, not_193_out, not_194_out, not_195_out,
       not_196_out, not_197_out, not_198_out, not_199_out, not_200_out, not_201_out, not_202_out,
       not_203_out, not_204_out, not_205_out, not_206_out, not_207_out, not_208_out, not_209_out,
       not_210_out, not_211_out, not_212_out, not_213_out, not_214_out, not_215_out, not_216_out,
       not_217_out, not_218_out, not_219_out, not_220_out, not_221_out, not_222_out, not_223_out,
       not_224_out, not_225_out, not_226_out, not_227_out, not_228_out, not_229_out, not_230_out,
       not_231_out, not_232_out, not_233_out, not_234_out, not_235_out, not_236_out;

  not not_1 (not_1_out, OP5);
  not not_2 (not_2_out, OP4);
  not not_3 (not_3_out, OP3);
  not not_4 (not_4_out, OP2);
  not not_5 (not_5_out, OP1);
  not not_6 (not_6_out, OP0);
  not not_7 (not_7_out, F5);
  not not_8 (not_8_out, F4);
  not not_9 (not_9_out, F3);
  not not_10 (not_10_out, F2);
  not not_11 (not_11_out, OP5);
  not not_12 (not_12_out, OP4);
  not not_13 (not_13_out, OP3);
  not not_14 (not_14_out, OP2);
  not not_15 (not_15_out, OP1);
  not not_16 (not_16_out, OP0);
  not not_17 (not_17_out, F4);
  not not_18 (not_18_out, F3);
  not not_19 (not_19_out, F2);
  not not_20 (not_20_out, F1);
  not not_21 (not_21_out, F0);
  not not_22 (not_22_out, OP5);
  not not_23 (not_23_out, OP4);
  not not_24 (not_24_out, OP3);
  not not_25 (not_25_out, OP2);
  not not_26 (not_26_out, OP1);
  not not_27 (not_27_out, OP0);
  not not_28 (not_28_out, F4);
  not not_29 (not_29_out, F3);
  not not_30 (not_30_out, F2);
  not not_31 (not_31_out, F1);
  not not_32 (not_32_out, OP5);
  not not_33 (not_33_out, OP4);
  not not_34 (not_34_out, OP3);
  not not_35 (not_35_out, OP2);
  not not_36 (not_36_out, OP1);
  not not_37 (not_37_out, OP0);
  not not_38 (not_38_out, F4);
  not not_39 (not_39_out, F3);
  not not_40 (not_40_out, F1);
  not not_41 (not_41_out, F0);
  not not_42 (not_42_out, OP5);
  not not_43 (not_43_out, OP4);
  not not_44 (not_44_out, OP3);
  not not_45 (not_45_out, OP2);
  not not_46 (not_46_out, OP1);
  not not_47 (not_47_out, OP0);
  not not_48 (not_48_out, F4);
  not not_49 (not_49_out, F2);
  not not_50 (not_50_out, F0);
  not not_51 (not_51_out, OP5);
  not not_52 (not_52_out, OP4);
  not not_53 (not_53_out, OP2);
  not not_54 (not_54_out, OP1);
  not not_55 (not_55_out, OP0);
  not not_56 (not_56_out, OP5);
  not not_57 (not_57_out, OP4);
  not not_58 (not_58_out, OP1);
  not not_59 (not_59_out, OP0);
  not not_60 (not_60_out, OP5);
  not not_61 (not_61_out, OP4);
  not not_62 (not_62_out, OP2);
  not not_63 (not_63_out, OP1);
  not not_64 (not_64_out, OP5);
  not not_65 (not_65_out, OP4);
  not not_66 (not_66_out, OP2);
  not not_67 (not_67_out, OP0);
  not not_68 (not_68_out, OP4);
  not not_69 (not_69_out, OP3);
  not not_70 (not_70_out, OP2);
  not not_71 (not_71_out, OP4);
  not not_72 (not_72_out, OP2);
  not not_73 (not_73_out, OP5);
  not not_74 (not_74_out, OP4);
  not not_75 (not_75_out, OP3);
  not not_76 (not_76_out, OP2);
  not not_77 (not_77_out, OP1);
  not not_78 (not_78_out, OP0);
  not not_79 (not_79_out, F5);
  not not_80 (not_80_out, F4);
  not not_81 (not_81_out, F3);
  not not_82 (not_82_out, F2);
  not not_83 (not_83_out, F0);
  not not_84 (not_84_out, OP5);
  not not_85 (not_85_out, OP4);
  not not_86 (not_86_out, OP3);
  not not_87 (not_87_out, OP2);
  not not_88 (not_88_out, OP1);
  not not_89 (not_89_out, OP0);
  not not_90 (not_90_out, F4);
  not not_91 (not_91_out, F3);
  not not_92 (not_92_out, F2);
  not not_93 (not_93_out, F0);
  not not_94 (not_94_out, OP5);
  not not_95 (not_95_out, OP4);
  not not_96 (not_96_out, OP3);
  not not_97 (not_97_out, OP2);
  not not_98 (not_98_out, OP1);
  not not_99 (not_99_out, OP0);
  not not_100 (not_100_out, F4);
  not not_101 (not_101_out, F3);
  not not_102 (not_102_out, F1);
  not not_103 (not_103_out, F0);
  not not_104 (not_104_out, OP5);
  not not_105 (not_105_out, OP4);
  not not_106 (not_106_out, OP3);
  not not_107 (not_107_out, OP2);
  not not_108 (not_108_out, OP1);
  not not_109 (not_109_out, OP0);
  not not_110 (not_110_out, F4);
  not not_111 (not_111_out, F3);
  not not_112 (not_112_out, OP5);
  not not_113 (not_113_out, OP4);
  not not_114 (not_114_out, OP3);
  not not_115 (not_115_out, OP2);
  not not_116 (not_116_out, OP1);
  not not_117 (not_117_out, OP0);
  not not_118 (not_118_out, F4);
  not not_119 (not_119_out, F2);
  not not_120 (not_120_out, F0);
  not not_121 (not_121_out, OP5);
  not not_122 (not_122_out, OP4);
  not not_123 (not_123_out, OP1);
  not not_124 (not_124_out, OP0);
  not not_125 (not_125_out, OP5);
  not not_126 (not_126_out, OP4);
  not not_127 (not_127_out, OP2);
  not not_128 (not_128_out, OP0);
  not not_129 (not_129_out, OP5);
  not not_130 (not_130_out, OP4);
  not not_131 (not_131_out, OP3);
  not not_132 (not_132_out, OP2);
  not not_133 (not_133_out, OP1);
  not not_134 (not_134_out, OP0);
  not not_135 (not_135_out, F4);
  not not_136 (not_136_out, F3);
  not not_137 (not_137_out, F2);
  not not_138 (not_138_out, F1);
  not not_139 (not_139_out, F0);
  not not_140 (not_140_out, OP5);
  not not_141 (not_141_out, OP4);
  not not_142 (not_142_out, OP3);
  not not_143 (not_143_out, OP2);
  not not_144 (not_144_out, OP1);
  not not_145 (not_145_out, OP0);
  not not_146 (not_146_out, F4);
  not not_147 (not_147_out, F3);
  not not_148 (not_148_out, F2);
  not not_149 (not_149_out, F1);
  not not_150 (not_150_out, OP5);
  not not_151 (not_151_out, OP4);
  not not_152 (not_152_out, OP3);
  not not_153 (not_153_out, OP2);
  not not_154 (not_154_out, OP1);
  not not_155 (not_155_out, OP0);
  not not_156 (not_156_out, F4);
  not not_157 (not_157_out, F3);
  not not_158 (not_158_out, F2);
  not not_159 (not_159_out, F0);
  not not_160 (not_160_out, OP5);
  not not_161 (not_161_out, OP4);
  not not_162 (not_162_out, OP3);
  not not_163 (not_163_out, OP2);
  not not_164 (not_164_out, OP1);
  not not_165 (not_165_out, OP0);
  not not_166 (not_166_out, F4);
  not not_167 (not_167_out, F3);
  not not_168 (not_168_out, F1);
  not not_169 (not_169_out, F0);
  not not_170 (not_170_out, OP5);
  not not_171 (not_171_out, OP4);
  not not_172 (not_172_out, OP3);
  not not_173 (not_173_out, OP2);
  not not_174 (not_174_out, OP1);
  not not_175 (not_175_out, OP0);
  not not_176 (not_176_out, F4);
  not not_177 (not_177_out, F2);
  not not_178 (not_178_out, OP5);
  not not_179 (not_179_out, OP4);
  not not_180 (not_180_out, OP2);
  not not_181 (not_181_out, OP1);
  not not_182 (not_182_out, OP0);
  not not_183 (not_183_out, OP5);
  not not_184 (not_184_out, OP4);
  not not_185 (not_185_out, OP1);
  not not_186 (not_186_out, OP0);
  not not_187 (not_187_out, OP5);
  not not_188 (not_188_out, OP4);
  not not_189 (not_189_out, OP2);
  not not_190 (not_190_out, OP1);
  not not_191 (not_191_out, OP4);
  not not_192 (not_192_out, OP3);
  not not_193 (not_193_out, OP2);
  not not_194 (not_194_out, OP4);
  not not_195 (not_195_out, OP2);
  not not_196 (not_196_out, OP5);
  not not_197 (not_197_out, OP4);
  not not_198 (not_198_out, OP3);
  not not_199 (not_199_out, OP2);
  not not_200 (not_200_out, OP1);
  not not_201 (not_201_out, OP0);
  not not_202 (not_202_out, F4);
  not not_203 (not_203_out, F3);
  not not_204 (not_204_out, F1);
  not not_205 (not_205_out, OP5);
  not not_206 (not_206_out, OP4);
  not not_207 (not_207_out, OP3);
  not not_208 (not_208_out, OP2);
  not not_209 (not_209_out, OP1);
  not not_210 (not_210_out, OP0);
  not not_211 (not_211_out, F4);
  not not_212 (not_212_out, F3);
  not not_213 (not_213_out, OP5);
  not not_214 (not_214_out, OP4);
  not not_215 (not_215_out, OP3);
  not not_216 (not_216_out, OP2);
  not not_217 (not_217_out, OP1);
  not not_218 (not_218_out, OP0);
  not not_219 (not_219_out, F4);
  not not_220 (not_220_out, F2);
  not not_221 (not_221_out, F0);
  not not_222 (not_222_out, OP5);
  not not_223 (not_223_out, OP4);
  not not_224 (not_224_out, OP3);
  not not_225 (not_225_out, OP2);
  not not_226 (not_226_out, OP1);
  not not_227 (not_227_out, OP0);
  not not_228 (not_228_out, F4);
  not not_229 (not_229_out, F2);
  not not_230 (not_230_out, OP5);
  not not_231 (not_231_out, OP4);
  not not_232 (not_232_out, OP2);
  not not_233 (not_233_out, OP0);
  not not_234 (not_234_out, OP5);
  not not_235 (not_235_out, OP4);
  not not_236 (not_236_out, OP1);
  and and_1 (and_1_out, not_1_out, not_2_out, not_3_out, not_4_out, not_5_out, not_6_out, not_7_out, not_8_out, not_9_out, not_10_out, F1, F0);
  and and_2 (and_2_out, not_11_out, not_12_out, not_13_out, not_14_out, not_15_out, not_16_out, F5, not_17_out, not_18_out, not_19_out, not_20_out, not_21_out);
  and and_3 (and_3_out, not_22_out, not_23_out, not_24_out, not_25_out, not_26_out, not_27_out, F5, not_28_out, not_29_out, not_30_out, not_31_out, F0);
  and and_4 (and_4_out, not_32_out, not_33_out, not_34_out, not_35_out, not_36_out, not_37_out, F5, not_38_out, not_39_out, F2, not_40_out, not_41_out);
  and and_5 (and_5_out, not_42_out, not_43_out, not_44_out, not_45_out, not_46_out, not_47_out, F5, not_48_out, F3, not_49_out, F1, not_50_out);
  and and_6 (and_6_out, not_51_out, not_52_out, OP3, not_53_out, not_54_out, not_55_out);
  and and_7 (and_7_out, not_56_out, not_57_out, OP3, OP2, not_58_out, not_59_out);
  and and_8 (and_8_out, not_60_out, not_61_out, OP3, not_62_out, not_63_out, OP0);
  and and_9 (and_9_out, not_64_out, not_65_out, OP3, not_66_out, OP1, not_67_out);
  and and_10 (and_10_out, OP5, not_68_out, not_69_out, not_70_out, OP1, OP0);
  and and_11 (and_11_out, OP5, not_71_out, OP3, not_72_out, OP1, OP0);
  and and_12 (and_12_out, not_73_out, not_74_out, not_75_out, not_76_out, not_77_out, not_78_out, not_79_out, not_80_out, not_81_out, not_82_out, F1, not_83_out);
  and and_13 (and_13_out, not_84_out, not_85_out, not_86_out, not_87_out, not_88_out, not_89_out, F5, not_90_out, not_91_out, not_92_out, F1, not_93_out);
  and and_14 (and_14_out, not_94_out, not_95_out, not_96_out, not_97_out, not_98_out, not_99_out, F5, not_100_out, not_101_out, F2, not_102_out, not_103_out);
  and and_15 (and_15_out, not_104_out, not_105_out, not_106_out, not_107_out, not_108_out, not_109_out, F5, not_110_out, not_111_out, F2, F1, F0);
  and and_16 (and_16_out, not_112_out, not_113_out, not_114_out, not_115_out, not_116_out, not_117_out, F5, not_118_out, F3, not_119_out, F1, not_120_out);
  and and_17 (and_17_out, not_121_out, not_122_out, OP3, OP2, not_123_out, not_124_out);
  and and_18 (and_18_out, not_125_out, not_126_out, OP3, not_127_out, OP1, not_128_out);
  and and_19 (and_19_out, not_129_out, not_130_out, not_131_out, not_132_out, not_133_out, not_134_out, F5, not_135_out, not_136_out, not_137_out, not_138_out, not_139_out);
  and and_20 (and_20_out, not_140_out, not_141_out, not_142_out, not_143_out, not_144_out, not_145_out, F5, not_146_out, not_147_out, not_148_out, not_149_out, F0);
  and and_21 (and_21_out, not_150_out, not_151_out, not_152_out, not_153_out, not_154_out, not_155_out, F5, not_156_out, not_157_out, not_158_out, F1, not_159_out);
  and and_22 (and_22_out, not_160_out, not_161_out, not_162_out, not_163_out, not_164_out, not_165_out, F5, not_166_out, not_167_out, F2, not_168_out, not_169_out);
  and and_23 (and_23_out, not_170_out, not_171_out, not_172_out, not_173_out, not_174_out, not_175_out, F5, not_176_out, F3, not_177_out, F1, F0);
  and and_24 (and_24_out, not_178_out, not_179_out, OP3, not_180_out, not_181_out, not_182_out);
  and and_25 (and_25_out, not_183_out, not_184_out, OP3, OP2, not_185_out, not_186_out);
  and and_26 (and_26_out, not_187_out, not_188_out, OP3, not_189_out, not_190_out, OP0);
  and and_27 (and_27_out, OP5, not_191_out, not_192_out, not_193_out, OP1, OP0);
  and and_28 (and_28_out, OP5, not_194_out, OP3, not_195_out, OP1, OP0);
  and and_29 (and_29_out, not_196_out, not_197_out, not_198_out, not_199_out, not_200_out, not_201_out, F5, not_202_out, not_203_out, F2, not_204_out, F0);
  and and_30 (and_30_out, not_205_out, not_206_out, not_207_out, not_208_out, not_209_out, not_210_out, F5, not_211_out, not_212_out, F2, F1, F0);
  and and_31 (and_31_out, not_213_out, not_214_out, not_215_out, not_216_out, not_217_out, not_218_out, F5, not_219_out, F3, not_220_out, F1, not_221_out);
  and and_32 (and_32_out, not_222_out, not_223_out, not_224_out, not_225_out, not_226_out, not_227_out, F5, not_228_out, F3, not_229_out, F1, F0);
  and and_33 (and_33_out, not_230_out, not_231_out, OP3, not_232_out, OP1, not_233_out);
  and and_34 (and_34_out, not_234_out, not_235_out, OP3, OP2, not_236_out, OP0);
  or or_1 (S0, and_1_out, and_2_out, and_3_out, and_4_out, and_5_out, and_6_out, and_7_out, and_8_out, and_9_out, and_10_out, and_11_out);
  or or_2 (S1, and_12_out, and_13_out, and_14_out, and_15_out, and_16_out, and_17_out, and_18_out);
  or or_3 (S2, and_19_out, and_20_out, and_21_out, and_22_out, and_23_out, and_24_out, and_25_out, and_26_out, and_27_out, and_28_out);
  or or_4 (S3, and_29_out, and_30_out, and_31_out, and_32_out, and_33_out, and_34_out);
endmodule

// 控制信号生成
module \控制信号自动生成  (
  input  OP0,
  input  OP1,
  input  OP2,
  input  OP3,
  input  OP4,
  input  OP5,
  input  F0,
  input  F1,
  input  F2,
  input  F3,
  input  F4,
  input  F5,
  output MemToReg,
  output MemWrite,
  output ALU_SRC,
  output RegWrite,
  output SysCALL,
  output SignedExt,
  output RegDst,
  output BEQ,
  output BNE,
  output JR,
  output JUMP,
  output JAL
);

  wire and_3_out, and_4_out, and_5_out, and_6_out, and_7_out, and_8_out, and_9_out, and_10_out, and_11_out,
       and_12_out, and_13_out, and_14_out, and_15_out, and_16_out, and_17_out, and_18_out, and_19_out,
       and_20_out, and_21_out, and_22_out, and_23_out, and_24_out, and_25_out, and_26_out, and_27_out,
       and_29_out, and_30_out, and_31_out, and_32_out, and_33_out, and_34_out, and_35_out, and_36_out,
       and_37_out, and_38_out, and_39_out, and_40_out, and_41_out, and_42_out, and_43_out, and_44_out,
       and_45_out, and_46_out, and_50_out, and_51_out, and_52_out, not_1_out, not_2_out, not_3_out,
       not_4_out, not_5_out, not_6_out, not_7_out, not_8_out, not_9_out, not_10_out, not_11_out, not_12_out,
       not_13_out, not_14_out, not_15_out, not_16_out, not_17_out, not_18_out, not_19_out, not_20_out,
       not_21_out, not_22_out, not_23_out, not_24_out, not_25_out, not_26_out, not_27_out, not_28_out,
       not_29_out, not_30_out, not_31_out, not_32_out, not_33_out, not_34_out, not_35_out, not_36_out,
       not_37_out, not_38_out, not_39_out, not_40_out, not_41_out, not_42_out, not_43_out, not_44_out,
       not_45_out, not_46_out, not_47_out, not_48_out, not_49_out, not_50_out, not_51_out, not_52_out,
       not_53_out, not_54_out, not_55_out, not_56_out, not_57_out, not_58_out, not_59_out, not_60_out,
       not_61_out, not_62_out, not_63_out, not_64_out, not_65_out, not_66_out, not_67_out, not_68_out,
       not_69_out, not_70_out, not_71_out, not_72_out, not_73_out, not_74_out, not_75_out, not_76_out,
       not_77_out, not_78_out, not_79_out, not_80_out, not_81_out, not_82_out, not_83_out, not_84_out,
       not_85_out, not_86_out, not_87_out, not_88_out, not_89_out, not_90_out, not_91_out, not_92_out,
       not_93_out, not_94_out, not_95_out, not_96_out, not_97_out, not_98_out, not_99_out, not_100_out,
       not_101_out, not_102_out, not_103_out, not_104_out, not_105_out, not_106_out, not_107_out,
       not_108_out, not_109_out, not_110_out, not_111_out, not_112_out, not_113_out, not_114_out,
       not_115_out, not_116_out, not_117_out, not_118_out, not_119_out, not_120_out, not_121_out,
       not_122_out, not_123_out, not_124_out, not_125_out, not_126_out, not_127_out, not_128_out,
       not_129_out, not_130_out, not_131_out, not_132_out, not_133_out, not_134_out, not_135_out,
       not_136_out, not_137_out, not_138_out, not_139_out, not_140_out, not_141_out, not_142_out,
       not_143_out, not_144_out, not_145_out, not_146_out, not_147_out, not_148_out, not_149_out,
       not_150_out, not_151_out, not_152_out, not_153_out, not_154_out, not_155_out, not_156_out,
       not_157_out, not_158_out, not_159_out, not_160_out, not_161_out, not_162_out, not_163_out,
       not_164_out, not_165_out, not_166_out, not_167_out, not_168_out, not_169_out, not_170_out,
       not_171_out, not_172_out, not_173_out, not_174_out, not_175_out, not_176_out, not_177_out,
       not_178_out, not_179_out, not_180_out, not_181_out, not_182_out, not_183_out, not_184_out,
       not_185_out, not_186_out, not_187_out, not_188_out, not_189_out, not_190_out, not_191_out,
       not_192_out, not_193_out, not_194_out, not_195_out, not_196_out, not_197_out, not_198_out,
       not_199_out, not_200_out, not_201_out, not_202_out, not_203_out, not_204_out, not_205_out,
       not_206_out, not_207_out, not_208_out, not_209_out, not_210_out, not_211_out, not_212_out,
       not_213_out, not_214_out, not_215_out, not_216_out, not_217_out, not_218_out, not_219_out,
       not_220_out, not_221_out, not_222_out, not_223_out, not_224_out, not_225_out, not_226_out,
       not_227_out, not_228_out, not_229_out, not_230_out, not_231_out, not_232_out, not_233_out,
       not_234_out, not_235_out, not_236_out, not_237_out, not_238_out, not_239_out, not_240_out,
       not_241_out, not_242_out, not_243_out, not_244_out, not_245_out, not_246_out, not_247_out,
       not_248_out, not_249_out, not_250_out, not_251_out, not_252_out, not_253_out, not_254_out,
       not_255_out, not_256_out, not_257_out, not_258_out, not_259_out, not_260_out, not_261_out,
       not_262_out, not_263_out, not_264_out, not_265_out, not_266_out, not_267_out, not_268_out,
       not_269_out, not_270_out, not_271_out, not_272_out, not_273_out, not_274_out, not_275_out,
       not_276_out, not_277_out, not_278_out, not_279_out, not_280_out, not_281_out, not_282_out,
       not_283_out, not_284_out, not_285_out, not_286_out, not_287_out, not_288_out, not_289_out,
       not_290_out, not_291_out, not_292_out, not_293_out, not_294_out, not_295_out, not_296_out,
       not_297_out, not_298_out, not_299_out, not_300_out, not_301_out, not_302_out, not_303_out,
       not_304_out, not_305_out, not_306_out, not_307_out, not_308_out, not_309_out, not_310_out,
       not_311_out, not_312_out, not_313_out, not_314_out, not_315_out, not_316_out, not_317_out,
       not_318_out, not_319_out, not_320_out, not_321_out, not_322_out, not_323_out, not_324_out,
       not_325_out, not_326_out, not_327_out, not_328_out, not_329_out, not_330_out, not_331_out,
       not_332_out, not_333_out, not_334_out, not_335_out, not_336_out, not_337_out, not_338_out,
       not_339_out, not_340_out, not_341_out, not_342_out, not_343_out, not_344_out, not_345_out,
       not_346_out, not_347_out, not_348_out, not_349_out, not_350_out, not_351_out, not_352_out,
       not_353_out, not_354_out;

  not not_1 (not_1_out, OP4);
  not not_2 (not_2_out, OP3);
  not not_3 (not_3_out, OP2);
  not not_4 (not_4_out, OP4);
  not not_5 (not_5_out, OP2);
  not not_6 (not_6_out, OP5);
  not not_7 (not_7_out, OP4);
  not not_8 (not_8_out, OP2);
  not not_9 (not_9_out, OP1);
  not not_10 (not_10_out, OP0);
  not not_11 (not_11_out, OP5);
  not not_12 (not_12_out, OP4);
  not not_13 (not_13_out, OP1);
  not not_14 (not_14_out, OP0);
  not not_15 (not_15_out, OP5);
  not not_16 (not_16_out, OP4);
  not not_17 (not_17_out, OP2);
  not not_18 (not_18_out, OP1);
  not not_19 (not_19_out, OP5);
  not not_20 (not_20_out, OP4);
  not not_21 (not_21_out, OP2);
  not not_22 (not_22_out, OP0);
  not not_23 (not_23_out, OP5);
  not not_24 (not_24_out, OP4);
  not not_25 (not_25_out, OP1);
  not not_26 (not_26_out, OP4);
  not not_27 (not_27_out, OP3);
  not not_28 (not_28_out, OP2);
  not not_29 (not_29_out, OP4);
  not not_30 (not_30_out, OP2);
  not not_31 (not_31_out, OP5);
  not not_32 (not_32_out, OP4);
  not not_33 (not_33_out, OP3);
  not not_34 (not_34_out, OP2);
  not not_35 (not_35_out, OP1);
  not not_36 (not_36_out, OP0);
  not not_37 (not_37_out, F5);
  not not_38 (not_38_out, F4);
  not not_39 (not_39_out, F3);
  not not_40 (not_40_out, F2);
  not not_41 (not_41_out, F1);
  not not_42 (not_42_out, F0);
  not not_43 (not_43_out, OP5);
  not not_44 (not_44_out, OP4);
  not not_45 (not_45_out, OP3);
  not not_46 (not_46_out, OP2);
  not not_47 (not_47_out, OP1);
  not not_48 (not_48_out, OP0);
  not not_49 (not_49_out, F5);
  not not_50 (not_50_out, F4);
  not not_51 (not_51_out, F3);
  not not_52 (not_52_out, F2);
  not not_53 (not_53_out, OP5);
  not not_54 (not_54_out, OP4);
  not not_55 (not_55_out, OP3);
  not not_56 (not_56_out, OP2);
  not not_57 (not_57_out, OP1);
  not not_58 (not_58_out, OP0);
  not not_59 (not_59_out, F5);
  not not_60 (not_60_out, F4);
  not not_61 (not_61_out, F3);
  not not_62 (not_62_out, F2);
  not not_63 (not_63_out, F0);
  not not_64 (not_64_out, OP5);
  not not_65 (not_65_out, OP4);
  not not_66 (not_66_out, OP3);
  not not_67 (not_67_out, OP2);
  not not_68 (not_68_out, OP1);
  not not_69 (not_69_out, OP0);
  not not_70 (not_70_out, F4);
  not not_71 (not_71_out, F3);
  not not_72 (not_72_out, F2);
  not not_73 (not_73_out, F1);
  not not_74 (not_74_out, F0);
  not not_75 (not_75_out, OP5);
  not not_76 (not_76_out, OP4);
  not not_77 (not_77_out, OP3);
  not not_78 (not_78_out, OP2);
  not not_79 (not_79_out, OP1);
  not not_80 (not_80_out, OP0);
  not not_81 (not_81_out, F4);
  not not_82 (not_82_out, F3);
  not not_83 (not_83_out, F2);
  not not_84 (not_84_out, F1);
  not not_85 (not_85_out, OP5);
  not not_86 (not_86_out, OP4);
  not not_87 (not_87_out, OP3);
  not not_88 (not_88_out, OP2);
  not not_89 (not_89_out, OP1);
  not not_90 (not_90_out, OP0);
  not not_91 (not_91_out, F4);
  not not_92 (not_92_out, F3);
  not not_93 (not_93_out, F2);
  not not_94 (not_94_out, F0);
  not not_95 (not_95_out, OP5);
  not not_96 (not_96_out, OP4);
  not not_97 (not_97_out, OP3);
  not not_98 (not_98_out, OP2);
  not not_99 (not_99_out, OP1);
  not not_100 (not_100_out, OP0);
  not not_101 (not_101_out, F4);
  not not_102 (not_102_out, F3);
  not not_103 (not_103_out, F1);
  not not_104 (not_104_out, F0);
  not not_105 (not_105_out, OP5);
  not not_106 (not_106_out, OP4);
  not not_107 (not_107_out, OP3);
  not not_108 (not_108_out, OP2);
  not not_109 (not_109_out, OP1);
  not not_110 (not_110_out, OP0);
  not not_111 (not_111_out, F4);
  not not_112 (not_112_out, F3);
  not not_113 (not_113_out, F1);
  not not_114 (not_114_out, OP5);
  not not_115 (not_115_out, OP4);
  not not_116 (not_116_out, OP3);
  not not_117 (not_117_out, OP2);
  not not_118 (not_118_out, OP1);
  not not_119 (not_119_out, OP0);
  not not_120 (not_120_out, F4);
  not not_121 (not_121_out, F3);
  not not_122 (not_122_out, OP5);
  not not_123 (not_123_out, OP4);
  not not_124 (not_124_out, OP3);
  not not_125 (not_125_out, OP2);
  not not_126 (not_126_out, OP1);
  not not_127 (not_127_out, OP0);
  not not_128 (not_128_out, F4);
  not not_129 (not_129_out, F2);
  not not_130 (not_130_out, F0);
  not not_131 (not_131_out, OP5);
  not not_132 (not_132_out, OP4);
  not not_133 (not_133_out, OP3);
  not not_134 (not_134_out, OP2);
  not not_135 (not_135_out, OP1);
  not not_136 (not_136_out, OP0);
  not not_137 (not_137_out, F4);
  not not_138 (not_138_out, F2);
  not not_139 (not_139_out, OP5);
  not not_140 (not_140_out, OP4);
  not not_141 (not_141_out, OP3);
  not not_142 (not_142_out, OP2);
  not not_143 (not_143_out, OP5);
  not not_144 (not_144_out, OP4);
  not not_145 (not_145_out, OP2);
  not not_146 (not_146_out, OP1);
  not not_147 (not_147_out, OP0);
  not not_148 (not_148_out, OP5);
  not not_149 (not_149_out, OP4);
  not not_150 (not_150_out, OP1);
  not not_151 (not_151_out, OP0);
  not not_152 (not_152_out, OP5);
  not not_153 (not_153_out, OP4);
  not not_154 (not_154_out, OP2);
  not not_155 (not_155_out, OP1);
  not not_156 (not_156_out, OP5);
  not not_157 (not_157_out, OP4);
  not not_158 (not_158_out, OP2);
  not not_159 (not_159_out, OP0);
  not not_160 (not_160_out, OP5);
  not not_161 (not_161_out, OP4);
  not not_162 (not_162_out, OP1);
  not not_163 (not_163_out, OP4);
  not not_164 (not_164_out, OP3);
  not not_165 (not_165_out, OP2);
  not not_166 (not_166_out, OP5);
  not not_167 (not_167_out, OP4);
  not not_168 (not_168_out, OP3);
  not not_169 (not_169_out, OP2);
  not not_170 (not_170_out, OP1);
  not not_171 (not_171_out, OP0);
  not not_172 (not_172_out, F5);
  not not_173 (not_173_out, F4);
  not not_174 (not_174_out, F1);
  not not_175 (not_175_out, F0);
  not not_176 (not_176_out, OP5);
  not not_177 (not_177_out, OP4);
  not not_178 (not_178_out, OP3);
  not not_179 (not_179_out, OP1);
  not not_180 (not_180_out, OP0);
  not not_181 (not_181_out, OP5);
  not not_182 (not_182_out, OP4);
  not not_183 (not_183_out, OP3);
  not not_184 (not_184_out, OP1);
  not not_185 (not_185_out, OP5);
  not not_186 (not_186_out, OP4);
  not not_187 (not_187_out, OP2);
  not not_188 (not_188_out, OP1);
  not not_189 (not_189_out, OP0);
  not not_190 (not_190_out, OP5);
  not not_191 (not_191_out, OP4);
  not not_192 (not_192_out, OP2);
  not not_193 (not_193_out, OP1);
  not not_194 (not_194_out, OP5);
  not not_195 (not_195_out, OP4);
  not not_196 (not_196_out, OP2);
  not not_197 (not_197_out, OP0);
  not not_198 (not_198_out, OP4);
  not not_199 (not_199_out, OP3);
  not not_200 (not_200_out, OP2);
  not not_201 (not_201_out, OP4);
  not not_202 (not_202_out, OP2);
  not not_203 (not_203_out, OP5);
  not not_204 (not_204_out, OP4);
  not not_205 (not_205_out, OP3);
  not not_206 (not_206_out, OP2);
  not not_207 (not_207_out, OP1);
  not not_208 (not_208_out, OP0);
  not not_209 (not_209_out, F5);
  not not_210 (not_210_out, F4);
  not not_211 (not_211_out, F3);
  not not_212 (not_212_out, F2);
  not not_213 (not_213_out, F1);
  not not_214 (not_214_out, F0);
  not not_215 (not_215_out, OP5);
  not not_216 (not_216_out, OP4);
  not not_217 (not_217_out, OP3);
  not not_218 (not_218_out, OP2);
  not not_219 (not_219_out, OP1);
  not not_220 (not_220_out, OP0);
  not not_221 (not_221_out, F5);
  not not_222 (not_222_out, F4);
  not not_223 (not_223_out, F3);
  not not_224 (not_224_out, F2);
  not not_225 (not_225_out, OP5);
  not not_226 (not_226_out, OP4);
  not not_227 (not_227_out, OP3);
  not not_228 (not_228_out, OP2);
  not not_229 (not_229_out, OP1);
  not not_230 (not_230_out, OP0);
  not not_231 (not_231_out, F5);
  not not_232 (not_232_out, F4);
  not not_233 (not_233_out, F3);
  not not_234 (not_234_out, F2);
  not not_235 (not_235_out, F0);
  not not_236 (not_236_out, OP5);
  not not_237 (not_237_out, OP4);
  not not_238 (not_238_out, OP3);
  not not_239 (not_239_out, OP2);
  not not_240 (not_240_out, OP1);
  not not_241 (not_241_out, OP0);
  not not_242 (not_242_out, F4);
  not not_243 (not_243_out, F3);
  not not_244 (not_244_out, F2);
  not not_245 (not_245_out, F1);
  not not_246 (not_246_out, F0);
  not not_247 (not_247_out, OP5);
  not not_248 (not_248_out, OP4);
  not not_249 (not_249_out, OP3);
  not not_250 (not_250_out, OP2);
  not not_251 (not_251_out, OP1);
  not not_252 (not_252_out, OP0);
  not not_253 (not_253_out, F4);
  not not_254 (not_254_out, F3);
  not not_255 (not_255_out, F2);
  not not_256 (not_256_out, F1);
  not not_257 (not_257_out, OP5);
  not not_258 (not_258_out, OP4);
  not not_259 (not_259_out, OP3);
  not not_260 (not_260_out, OP2);
  not not_261 (not_261_out, OP1);
  not not_262 (not_262_out, OP0);
  not not_263 (not_263_out, F4);
  not not_264 (not_264_out, F3);
  not not_265 (not_265_out, F2);
  not not_266 (not_266_out, F0);
  not not_267 (not_267_out, OP5);
  not not_268 (not_268_out, OP4);
  not not_269 (not_269_out, OP3);
  not not_270 (not_270_out, OP2);
  not not_271 (not_271_out, OP1);
  not not_272 (not_272_out, OP0);
  not not_273 (not_273_out, F4);
  not not_274 (not_274_out, F3);
  not not_275 (not_275_out, F1);
  not not_276 (not_276_out, F0);
  not not_277 (not_277_out, OP5);
  not not_278 (not_278_out, OP4);
  not not_279 (not_279_out, OP3);
  not not_280 (not_280_out, OP2);
  not not_281 (not_281_out, OP1);
  not not_282 (not_282_out, OP0);
  not not_283 (not_283_out, F4);
  not not_284 (not_284_out, F3);
  not not_285 (not_285_out, F1);
  not not_286 (not_286_out, OP5);
  not not_287 (not_287_out, OP4);
  not not_288 (not_288_out, OP3);
  not not_289 (not_289_out, OP2);
  not not_290 (not_290_out, OP1);
  not not_291 (not_291_out, OP0);
  not not_292 (not_292_out, F4);
  not not_293 (not_293_out, F3);
  not not_294 (not_294_out, OP5);
  not not_295 (not_295_out, OP4);
  not not_296 (not_296_out, OP3);
  not not_297 (not_297_out, OP2);
  not not_298 (not_298_out, OP1);
  not not_299 (not_299_out, OP0);
  not not_300 (not_300_out, F4);
  not not_301 (not_301_out, F2);
  not not_302 (not_302_out, F0);
  not not_303 (not_303_out, OP5);
  not not_304 (not_304_out, OP4);
  not not_305 (not_305_out, OP3);
  not not_306 (not_306_out, OP2);
  not not_307 (not_307_out, OP1);
  not not_308 (not_308_out, OP0);
  not not_309 (not_309_out, F4);
  not not_310 (not_310_out, F2);
  not not_311 (not_311_out, OP5);
  not not_312 (not_312_out, OP4);
  not not_313 (not_313_out, OP3);
  not not_314 (not_314_out, OP1);
  not not_315 (not_315_out, OP0);
  not not_316 (not_316_out, OP5);
  not not_317 (not_317_out, OP4);
  not not_318 (not_318_out, OP3);
  not not_319 (not_319_out, OP1);
  not not_320 (not_320_out, OP5);
  not not_321 (not_321_out, OP4);
  not not_322 (not_322_out, OP3);
  not not_323 (not_323_out, OP2);
  not not_324 (not_324_out, OP1);
  not not_325 (not_325_out, OP0);
  not not_326 (not_326_out, F5);
  not not_327 (not_327_out, F4);
  not not_328 (not_328_out, F2);
  not not_329 (not_329_out, F1);
  not not_330 (not_330_out, F0);
  not not_331 (not_331_out, OP5);
  not not_332 (not_332_out, OP4);
  not not_333 (not_333_out, OP3);
  not not_334 (not_334_out, OP2);
  not not_335 (not_335_out, OP1);
  not not_336 (not_336_out, OP0);
  not not_337 (not_337_out, F5);
  not not_338 (not_338_out, F4);
  not not_339 (not_339_out, F2);
  not not_340 (not_340_out, F1);
  not not_341 (not_341_out, F0);
  not not_342 (not_342_out, OP5);
  not not_343 (not_343_out, OP4);
  not not_344 (not_344_out, OP3);
  not not_345 (not_345_out, OP2);
  not not_346 (not_346_out, OP0);
  not not_347 (not_347_out, OP5);
  not not_348 (not_348_out, OP4);
  not not_349 (not_349_out, OP3);
  not not_350 (not_350_out, OP2);
  not not_351 (not_351_out, OP5);
  not not_352 (not_352_out, OP4);
  not not_353 (not_353_out, OP3);
  not not_354 (not_354_out, OP2);
  and and_1 (MemToReg, OP5, not_1_out, not_2_out, not_3_out, OP1, OP0);
  and and_2 (MemWrite, OP5, not_4_out, OP3, not_5_out, OP1, OP0);
  and and_3 (and_3_out, not_6_out, not_7_out, OP3, not_8_out, not_9_out, not_10_out);
  and and_4 (and_4_out, not_11_out, not_12_out, OP3, OP2, not_13_out, not_14_out);
  and and_5 (and_5_out, not_15_out, not_16_out, OP3, not_17_out, not_18_out, OP0);
  and and_6 (and_6_out, not_19_out, not_20_out, OP3, not_21_out, OP1, not_22_out);
  and and_7 (and_7_out, not_23_out, not_24_out, OP3, OP2, not_25_out, OP0);
  and and_8 (and_8_out, OP5, not_26_out, not_27_out, not_28_out, OP1, OP0);
  and and_9 (and_9_out, OP5, not_29_out, OP3, not_30_out, OP1, OP0);
  and and_10 (and_10_out, not_31_out, not_32_out, not_33_out, not_34_out, not_35_out, not_36_out, not_37_out, not_38_out, not_39_out, not_40_out, not_41_out, not_42_out);
  and and_11 (and_11_out, not_43_out, not_44_out, not_45_out, not_46_out, not_47_out, not_48_out, not_49_out, not_50_out, not_51_out, not_52_out, F1, F0);
  and and_12 (and_12_out, not_53_out, not_54_out, not_55_out, not_56_out, not_57_out, not_58_out, not_59_out, not_60_out, not_61_out, not_62_out, F1, not_63_out);
  and and_13 (and_13_out, not_64_out, not_65_out, not_66_out, not_67_out, not_68_out, not_69_out, F5, not_70_out, not_71_out, not_72_out, not_73_out, not_74_out);
  and and_14 (and_14_out, not_75_out, not_76_out, not_77_out, not_78_out, not_79_out, not_80_out, F5, not_81_out, not_82_out, not_83_out, not_84_out, F0);
  and and_15 (and_15_out, not_85_out, not_86_out, not_87_out, not_88_out, not_89_out, not_90_out, F5, not_91_out, not_92_out, not_93_out, F1, not_94_out);
  and and_16 (and_16_out, not_95_out, not_96_out, not_97_out, not_98_out, not_99_out, not_100_out, F5, not_101_out, not_102_out, F2, not_103_out, not_104_out);
  and and_17 (and_17_out, not_105_out, not_106_out, not_107_out, not_108_out, not_109_out, not_110_out, F5, not_111_out, not_112_out, F2, not_113_out, F0);
  and and_18 (and_18_out, not_114_out, not_115_out, not_116_out, not_117_out, not_118_out, not_119_out, F5, not_120_out, not_121_out, F2, F1, F0);
  and and_19 (and_19_out, not_122_out, not_123_out, not_124_out, not_125_out, not_126_out, not_127_out, F5, not_128_out, F3, not_129_out, F1, not_130_out);
  and and_20 (and_20_out, not_131_out, not_132_out, not_133_out, not_134_out, not_135_out, not_136_out, F5, not_137_out, F3, not_138_out, F1, F0);
  and and_21 (and_21_out, not_139_out, not_140_out, not_141_out, not_142_out, OP1, OP0);
  and and_22 (and_22_out, not_143_out, not_144_out, OP3, not_145_out, not_146_out, not_147_out);
  and and_23 (and_23_out, not_148_out, not_149_out, OP3, OP2, not_150_out, not_151_out);
  and and_24 (and_24_out, not_152_out, not_153_out, OP3, not_154_out, not_155_out, OP0);
  and and_25 (and_25_out, not_156_out, not_157_out, OP3, not_158_out, OP1, not_159_out);
  and and_26 (and_26_out, not_160_out, not_161_out, OP3, OP2, not_162_out, OP0);
  and and_27 (and_27_out, OP5, not_163_out, not_164_out, not_165_out, OP1, OP0);
  and and_28 (SysCALL, not_166_out, not_167_out, not_168_out, not_169_out, not_170_out, not_171_out, not_172_out, not_173_out, F3, F2, not_174_out, not_175_out);
  and and_29 (and_29_out, not_176_out, not_177_out, not_178_out, OP2, not_179_out, not_180_out);
  and and_30 (and_30_out, not_181_out, not_182_out, not_183_out, OP2, not_184_out, OP0);
  and and_31 (and_31_out, not_185_out, not_186_out, OP3, not_187_out, not_188_out, not_189_out);
  and and_32 (and_32_out, not_190_out, not_191_out, OP3, not_192_out, not_193_out, OP0);
  and and_33 (and_33_out, not_194_out, not_195_out, OP3, not_196_out, OP1, not_197_out);
  and and_34 (and_34_out, OP5, not_198_out, not_199_out, not_200_out, OP1, OP0);
  and and_35 (and_35_out, OP5, not_201_out, OP3, not_202_out, OP1, OP0);
  and and_36 (and_36_out, not_203_out, not_204_out, not_205_out, not_206_out, not_207_out, not_208_out, not_209_out, not_210_out, not_211_out, not_212_out, not_213_out, not_214_out);
  and and_37 (and_37_out, not_215_out, not_216_out, not_217_out, not_218_out, not_219_out, not_220_out, not_221_out, not_222_out, not_223_out, not_224_out, F1, F0);
  and and_38 (and_38_out, not_225_out, not_226_out, not_227_out, not_228_out, not_229_out, not_230_out, not_231_out, not_232_out, not_233_out, not_234_out, F1, not_235_out);
  and and_39 (and_39_out, not_236_out, not_237_out, not_238_out, not_239_out, not_240_out, not_241_out, F5, not_242_out, not_243_out, not_244_out, not_245_out, not_246_out);
  and and_40 (and_40_out, not_247_out, not_248_out, not_249_out, not_250_out, not_251_out, not_252_out, F5, not_253_out, not_254_out, not_255_out, not_256_out, F0);
  and and_41 (and_41_out, not_257_out, not_258_out, not_259_out, not_260_out, not_261_out, not_262_out, F5, not_263_out, not_264_out, not_265_out, F1, not_266_out);
  and and_42 (and_42_out, not_267_out, not_268_out, not_269_out, not_270_out, not_271_out, not_272_out, F5, not_273_out, not_274_out, F2, not_275_out, not_276_out);
  and and_43 (and_43_out, not_277_out, not_278_out, not_279_out, not_280_out, not_281_out, not_282_out, F5, not_283_out, not_284_out, F2, not_285_out, F0);
  and and_44 (and_44_out, not_286_out, not_287_out, not_288_out, not_289_out, not_290_out, not_291_out, F5, not_292_out, not_293_out, F2, F1, F0);
  and and_45 (and_45_out, not_294_out, not_295_out, not_296_out, not_297_out, not_298_out, not_299_out, F5, not_300_out, F3, not_301_out, F1, not_302_out);
  and and_46 (and_46_out, not_303_out, not_304_out, not_305_out, not_306_out, not_307_out, not_308_out, F5, not_309_out, F3, not_310_out, F1, F0);
  and and_47 (BEQ, not_311_out, not_312_out, not_313_out, OP2, not_314_out, not_315_out);
  and and_48 (BNE, not_316_out, not_317_out, not_318_out, OP2, not_319_out, OP0);
  and and_49 (JR, not_320_out, not_321_out, not_322_out, not_323_out, not_324_out, not_325_out, not_326_out, not_327_out, F3, not_328_out, not_329_out, not_330_out);
  and and_50 (and_50_out, not_331_out, not_332_out, not_333_out, not_334_out, not_335_out, not_336_out, not_337_out, not_338_out, F3, not_339_out, not_340_out, not_341_out);
  and and_51 (and_51_out, not_342_out, not_343_out, not_344_out, not_345_out, OP1, not_346_out);
  and and_52 (and_52_out, not_347_out, not_348_out, not_349_out, not_350_out, OP1, OP0);
  and and_53 (JAL, not_351_out, not_352_out, not_353_out, not_354_out, OP1, OP0);
  or or_1 (ALU_SRC, and_3_out, and_4_out, and_5_out, and_6_out, and_7_out, and_8_out, and_9_out);
  or or_2 (SignedExt, and_29_out, and_30_out, and_31_out, and_32_out, and_33_out, and_34_out, and_35_out);
  or or_3 (RegDst, and_36_out, and_37_out, and_38_out, and_39_out, and_40_out, and_41_out, and_42_out, and_43_out, and_44_out, and_45_out, and_46_out);
  or or_4 (JUMP, and_50_out, and_51_out, and_52_out);
  or or_5 (RegWrite, and_10_out, and_11_out, and_12_out, and_13_out, and_14_out, and_15_out, and_16_out, and_17_out, and_18_out, and_19_out, and_20_out, and_21_out, and_22_out, and_23_out, and_24_out, and_25_out, and_26_out, and_27_out);
endmodule

// ALU
module MIPS_ALU (
  input  [4:0] shamt,
  input  [31:0] X,
  input  [31:0] Y,
  input  [3:0] AluOP,
  output Equal,
  output [31:0] Result,
  output [31:0] Result_2
);

  wire [0:0] comparator_1_lt, comparator_2_lt;
  wire [31:0] adder_1_out, AND_out, divider_1_out, divider_1_rem, multiplier_1_cout, multiplier_1_out,
       NOR_out, OR_out, shifter_1_out, shifter_2_out, shifter_3_out, subtractor_1_out, XOR_out;

  assign AND_out = X & Y;  // AND_Gate AND, 32 bits wide
  assign OR_out = X | Y;  // OR_Gate OR, 32 bits wide
  Shifter #(.width(32), .shift("ll")) shifter_1 (.in(Y), .\dist (shamt), .out(shifter_1_out));
  Shifter #(.width(32), .shift("ar")) shifter_2 (.in(Y), .\dist (shamt), .out(shifter_2_out));
  Shifter #(.width(32), .shift("lr")) shifter_3 (.in(Y), .\dist (shamt), .out(shifter_3_out));
  Multiplier #(.width(32)) multiplier_1 (.a(X), .b(Y), .out(multiplier_1_out), .cout(multiplier_1_cout));  // open: cin
  Divider #(.width(32)) divider_1 (.a(X), .b(Y), .out(divider_1_out), .rem(divider_1_rem));  // open: upper
  Adder #(.width(32)) adder_1 (.a(X), .b(Y), .out(adder_1_out));  // open: cin, cout
  Subtractor #(.width(32)) subtractor_1 (.a(X), .b(Y), .out(subtractor_1_out));  // open: bin, bout
  assign XOR_out = X ^ Y;  // XOR_Gate XOR, 32 bits wide
  assign NOR_out = ~(X | Y);  // NOR_Gate NOR, 32 bits wide
  Comparator #(.width(32), .mode("twosComplement")) comparator_1 (
    .a(X), .b(Y), .eq(Equal), .lt(comparator_1_lt[0]));  // open: gt
  Comparator #(.width(32), .mode("unsigned")) comparator_2 (.a(X), .b(Y), .lt(comparator_2_lt[0]));  // open: gt, eq
  Multiplexer #(.select(4), .width(32), .disabled("Z"), .enable("false")) multiplexer_1 (
    .in0(shifter_1_out), .in1(shifter_2_out), .in2(shifter_3_out), .in3(multiplier_1_out),
    .in4(divider_1_out), .in5(adder_1_out), .in6(subtractor_1_out), .in7(AND_out), .in8(OR_out),
    .in9(XOR_out), .in10(NOR_out), .in11({{31{1'b0}}, comparator_1_lt[0]}),
    .in12({{31{1'b0}}, comparator_2_lt[0]}), .in13({32{1'b0}}), .in14({32{1'b0}}), .in15({32{1'b0}}),
    .out(Result), .sel(AluOP));
  Multiplexer #(.select(4), .width(32), .disabled("Z"), .enable("false")) multiplexer_2 (
    .in0({32{1'b0}}), .in1({32{1'b0}}), .in2({32{1'b0}}), .in3(multiplier_1_cout), .in4(divider_1_rem),
    .in5({32{1'b0}}), .in6({32{1'b0}}), .in7({32{1'b0}}), .in8({32{1'b0}}), .in9({32{1'b0}}),
    .in10({32{1'b0}}), .in11({32{1'b0}}), .in12({32{1'b0}}), .in13({32{1'b0}}), .in14({32{1'b0}}),
    .in15({32{1'b0}}), .out(Result_2), .sel(AluOP));

  // Other names for the same wires on the sheet: Result2[31:0] = Result_2; S[3:0] = AluOP

  // Notes on the sheet:
  //   不要改变此引脚区域内容，也不要改变ALU封装形式
  //   输入引脚
  //   输出引脚
endmodule

module MIPS_Regifile (
  input  [31:0] Din,
  input  Clk,
  input  WE,
  input  [4:0] R1_num,
  input  [4:0] W_num,
  input  [4:0] R2_num,
  output [31:0] R1,
  output [31:0] R2
);

  // RegisterFile registerfile_1: pin names not known; wires that end beside it: Din, Clk, WE, W_num, R1_num, R2_num, R1, R2
endmodule

module \理想流水线  (
  output RegWrite,
  output MemWrite,
  output [31:0] IF_PC,
  output [31:0] ID_PC,
  output [31:0] EX_PC,
  output [31:0] M_PC,
  output [31:0] WB_PC,
  output [31:0] RDin,
  output [31:0] MDin,
  output [31:0] LedData,
  output [31:0] v0,
  output [31:0] a0
);

  wire AluSrcB, and_1_out, and_2_out, Beq, BeqOut, Bne, BneOut, CLK, clock_1_out, clock_2_out,
       comparator_1_eq, comparator_1_lt, comparator_2_eq, d_ff_1_q, equal, EX_MEM_mentoregout,
       EX_MEM_regwriteout, Go, Halt, ID_EX_alusrcbout, ID_EX_memtoregout, ID_EX_memwriteout,
       ID_EX_regwriteout, ID_MemWrite, ID_RegWrite, IR1, IR2, IR3, JAL, JMP, JMPOut, JR, JROut,
       MEM_WB_mentoregout, MemToReg, multiplexer_1_out, nand_1_out, not_1_out, not_2_out, not_3_out, RegDst,
       register_1_q, register_2_q, RST, SignedExt, Syscall, SyscallOut, W1, W2, W3;
  wire [3:0] AluOP, ID_EX_aluopout;
  wire [4:0] EX_MEM_w_out, ID_EX_shamtout, ID_EX_w_out, MEM_WB_w_out, multiplexer_3_out, multiplexer_5_out,
       rd, rs_t, rt, shamt;
  wire [5:0] Func, OP;
  wire [12:0] CNT_num;
  wire [15:0] \LoadUse次数 , \总周期数 , \插入气泡数 , \无条件分支数 , \条件分支成功数 ;
  wire [31:0] adder_1_out, adder_2_out, bit_extender_1_out, bit_extender_2_out, EX_MEM_aluout_2, ID_EX_bout,
       ID_EX_immout, ID_EX_pcout, IF_ID_pc_4out, JAddr, MEM_WB_aluout_2, MEM_WB_menout, mips_alu_1_result,
       mips_regifile_1_r1, mips_regifile_1_r2, multiplexer_2_out, multiplexer_4_out, multiplexer_6_out,
       ram_1_data, rom_1_data, shifter_1_out;

  Button \u_总复位  (.out(RST));
  Button _1 (.out(IR1));
  Button _2 (.out(IR2));
  Button _3 (.out(IR3));
  Button \u_继续运行  (.out(Go));
  LED #(.active("true")) led_1 (.in(W1));
  LED #(.active("true")) led_2 (.in(W2));
  LED #(.active("true")) led_3 (.in(W3));
  D_Flip_Flop #(.trigger("high"), .Pre_Clr_Positions("LEGACY"), .NegatePresetClear("false"), .enable("true"), .NewFFLayout("false")) d_ff_1 (.Q(d_ff_1_q));  // open: clk, D, Qn, preset, en, reset
  // Probe on 13'hc
  Hex_Digit_Display hex_digit_display_1 (.value(LedData[31:28]));  // open: dp
  Comparator #(.width(13), .mode("twosComplement")) comparator_1 (
    .a(CNT_num), .b(13'hc), .eq(comparator_1_eq), .lt(comparator_1_lt));  // open: gt
  Clock #(.highDuration(1), .lowDuration(1)) clock_1 (.out(clock_1_out));
  Multiplexer #(.select(1), .width(1), .disabled("Z"), .enable("false")) multiplexer_1 (
    .in0(BneOut), .in1(BeqOut), .out(multiplexer_1_out), .sel(equal));
  Multiplexer #(.select(1), .width(32), .disabled("Z"), .enable("false")) multiplexer_2 (
    .in0(adder_1_out), .in1(adder_2_out), .out(multiplexer_2_out), .sel(multiplexer_1_out));
  not not_1 (not_1_out, SyscallOut);
  Hex_Digit_Display hex_digit_display_2 (.value(LedData[27:24]));  // open: dp
  Hex_Digit_Display hex_digit_display_3 (.value(LedData[23:20]));  // open: dp
  nand nand_1 (nand_1_out, d_ff_1_q, comparator_1_eq);
  Counter #(.width(13), .max('h1fff), .ongoal("stay"), .trigger("rising"), .behavior("old")) counter_1 (
    .count(comparator_1_lt), .Q(CNT_num), .clk(clock_1_out));  // open: load, D, carry, clr, preset
  Register #(.width(32), .trigger("rising"), .Select("low")) PC (
    .D(multiplexer_2_out), .en(not_1_out), .Q(IF_PC), .clk(CLK));  // open: clr
  Counter #(.width(16), .max('hffff), .ongoal("wrap"), .trigger("rising"), .behavior("old")) counter_2 (
    .count(not_1_out), .Q(\总周期数 ), .clk(CLK), .clr(RST));  // open: load, D, carry, preset
  Hex_Digit_Display hex_digit_display_4 (.value(LedData[15:12]));  // open: dp
  Hex_Digit_Display hex_digit_display_5 (.value(LedData[19:16]));  // open: dp
  assign CLK = nand_1_out ? clock_1_out : 1'bz;  // Controlled_Buffer controlled_buffer_1
  Hex_Digit_Display hex_digit_display_6 (.value(LedData[7:4]));  // open: dp
  Hex_Digit_Display hex_digit_display_7 (.value(LedData[11:8]));  // open: dp
  Clock #(.highDuration(1), .lowDuration(1)) clock_2 (.out(clock_2_out));
  Pull_Resistor #(.pull(1)) pull_resistor_1 (.node(CLK));
  Adder #(.width(32)) adder_1 (.a(IF_PC), .b(32'h4), .out(adder_1_out));  // open: cin, cout
  Hex_Digit_Display hex_digit_display_8 (.value(LedData[3:0]));  // open: dp
  ROM #(.addrWidth(10), .dataWidth(32), .Select("high")) rom_1 (.addr(IF_PC[11:2]), .data(rom_1_data));
  // Probe on \总周期数 
  IF_ID IF_ID (
    .PC_4(adder_1_out), .RD(rom_1_data), .JAddr(IF_PC), .CLK(CLK), .PC_4Out(IF_ID_pc_4out),
    .RDOut({OP, rs_t, rt, rd, shamt, Func}), .JAddrOut(ID_PC));  // open: 同步清零_高电平有效, 使能端_低电平有效
  // Probe on \总周期数 
  // Probe on \无条件分支数 
  // Probe on \条件分支成功数 
  // Probe on \插入气泡数 
  // Probe on \LoadUse次数 
  // Probe on IF_PC[11:0]
  \单周期硬布线控制器  \u_单周期硬布线控制器_1  (
    .Func(Func), .OP(OP), .ALU_OP(AluOP), .MemToReg(MemToReg), .MemWrite(ID_MemWrite), .ALU_SRC(AluSrcB),
    .RegWrite(ID_RegWrite), .SysCALL(Syscall), .SignedExt(SignedExt), .RegDst(RegDst), .JR(JR), .JMP(JMP),
    .Beq(Beq), .JAL(JAL), .Bne(Bne));
  // Probe on EX_PC[11:0]
  // Probe on ID_PC[11:0]
  Multiplexer #(.select(1), .width(5), .disabled("Z"), .enable("false")) multiplexer_3 (
    .in0(rt), .in1(rd), .out(multiplexer_3_out), .sel(RegDst));
  // Probe on M_PC[11:0]
  MIPS_Regifile mips_regifile_1 (
    .Din(RDin), .Clk(CLK), .R1(mips_regifile_1_r1), .R2(mips_regifile_1_r2), .WE(RegWrite),
    .W_num(MEM_WB_w_out), .R1_num(rs_t), .R2_num(rt));
  assign bit_extender_1_out = {{16{1'b0}}, {rd, shamt, Func}};  // Bit_Extender bit_extender_1
  Multiplexer #(.select(1), .width(32), .disabled("Z"), .enable("false")) multiplexer_4 (
    .in0(bit_extender_1_out), .in1(bit_extender_2_out), .out(multiplexer_4_out), .sel(SignedExt));
  assign bit_extender_2_out = {{16{rd[4]}}, {rd, shamt, Func}};  // Bit_Extender bit_extender_2
  Multiplexer #(.select(1), .width(5), .disabled("Z"), .enable("false")) multiplexer_5 (
    .in0(multiplexer_3_out), .in1({5{1'b1}}), .out(multiplexer_5_out), .sel(JAL));
  // Probe on WB_PC[11:0]
  Register #(.width(1), .trigger("rising"), .Select("low")) register_1 (
    .D(Syscall), .Q(register_1_q), .clk(CLK));  // open: en, clr
  ID_EX ID_EX (
    .RegWrite(ID_RegWrite), .AluOP(AluOP), .MemToReg(MemToReg), .AluSrcB(AluSrcB), .PC(IF_ID_pc_4out),
    .A(mips_regifile_1_r1), .B(mips_regifile_1_r2), .Imm(multiplexer_4_out), .Shamt(shamt),
    .W_num(multiplexer_5_out), .MemWrite(ID_MemWrite), .JMP(JMP), .Beq(Beq), .Bne(Bne), .CLK(CLK),
    .RegWriteOut(ID_EX_regwriteout), .AluOPOut(ID_EX_aluopout), .MemToRegOut(ID_EX_memtoregout),
    .AluSrcBOut(ID_EX_alusrcbout), .PCOut(ID_EX_pcout), .AOut(v0), .BOut(ID_EX_bout), .ImmOut(ID_EX_immout),
    .ShamtOut(ID_EX_shamtout), .W_Out(ID_EX_w_out), .MemWriteOut(ID_EX_memwriteout), .JMPOut(JMPOut),
    .BeqOut(BeqOut), .BneOut(BneOut), .JAddr({ID_PC[31:28], rs_t, rt, rd, shamt, Func, 2'b00}),
    .JAddr_2(JAddr), .JR(JR), .JROut(JROut), .ID_PC(ID_PC), .EX_PC(EX_PC));  // open: 同步清零_高电平有效, 使能端_低电平有效, JAL, JALOut, Syscall, EX_SysCall, Op, OpOut, DataRedirect, DataDirectOut
  Register #(.width(1), .trigger("rising"), .Select("low")) register_2 (
    .D(register_1_q), .Q(register_2_q), .clk(CLK));  // open: en, clr
  Shifter #(.width(32), .shift("ll")) shifter_1 (.in(ID_EX_immout), .\dist (5'b00010), .out(shifter_1_out));
  Multiplexer #(.select(1), .width(32), .disabled("Z"), .enable("false")) multiplexer_6 (
    .in0(ID_EX_bout), .in1(ID_EX_immout), .out(multiplexer_6_out), .sel(ID_EX_alusrcbout));
  Register #(.width(1), .trigger("rising"), .Select("low")) register_3 (
    .D(register_2_q), .en(not_2_out), .Q(SyscallOut), .clk(CLK));  // open: clr
  not not_2 (not_2_out, SyscallOut);
  Adder #(.width(32)) adder_2 (.a(ID_EX_pcout), .b(shifter_1_out), .out(adder_2_out));  // open: cin, cout
  MIPS_ALU mips_alu_1 (
    .X(v0), .Y(multiplexer_6_out), .AluOP(ID_EX_aluopout), .Equal(equal), .Result(mips_alu_1_result),
    .shamt(ID_EX_shamtout));  // open: Result_2
  EX_MEM EX_MEM (
    .RegWrite(ID_EX_regwriteout), .MenToReg(ID_EX_memtoregout), .AluOut(mips_alu_1_result), .B(ID_EX_bout),
    .W_num(ID_EX_w_out), .MemWrite(ID_EX_memwriteout), .CLK(CLK), .RegWriteOut(EX_MEM_regwriteout),
    .MenToRegOut(EX_MEM_mentoregout), .AluOut_2(EX_MEM_aluout_2), .BOut(MDin), .W_Out(EX_MEM_w_out),
    .MemWriteOut(MemWrite), .EX_PC(EX_PC), .MEM_PC(M_PC));  // open: 同步清零_高电平有效, 使能端_低电平有效, JAL, JALOut, PC_4, PCOut, EX_Halt, MEM_Halt, Op, OpOut
  RAM #(.addrWidth(10), .dataWidth(32), .bus("separate"), .Select("high")) ram_1 (
    .addr(EX_MEM_aluout_2[11:2]), .din(MDin), .data(ram_1_data), .str(MemWrite), .clk(CLK), .clr(RST));  // open: sel, ld
  MEM_WB MEM_WB (
    .RegWrite(EX_MEM_regwriteout), .MenToReg(EX_MEM_mentoregout), .MemOut(ram_1_data),
    .AluOut(EX_MEM_aluout_2), .W_num(EX_MEM_w_out), .CLK(CLK), .RegWriteOut(RegWrite),
    .MenToRegOut(MEM_WB_mentoregout), .MenOut(MEM_WB_menout), .AluOut_2(MEM_WB_aluout_2),
    .W_Out(MEM_WB_w_out), .MEM_PC(M_PC), .WB_PC(WB_PC));  // open: 同步清零_高电平有效, 使能端_低电平有效, JAL, JALOut, PC_4, PCOut, MEM_Halt, WB_Halt, Op, OpOut
  Multiplexer #(.select(1), .width(32), .disabled("Z"), .enable("false")) multiplexer_7 (
    .in0(MEM_WB_aluout_2), .in1(MEM_WB_menout), .out(RDin), .sel(MEM_WB_mentoregout));
  Comparator #(.width(32), .mode("twosComplement")) comparator_2 (
    .a(v0), .b(32'h32), .eq(comparator_2_eq));  // open: gt, lt
  not not_3 (not_3_out, comparator_2_eq);
  and and_1 (and_1_out, not_3_out, SyscallOut);
  and and_2 (and_2_out, SyscallOut, comparator_2_eq);
  Register #(.width(32), .trigger("rising"), .Select("low")) register_4 (
    .D(a0), .en(and_1_out), .Q(LedData), .clk(CLK));  // open: clr
  Register #(.width(1), .trigger("rising"), .Select("low")) register_5 (
    .D(and_2_out), .en(and_2_out), .Q(Halt), .clk(CLK), .clr(Go));

  // Other names for the same wires on the sheet: MEM_PC[31:0] = M_PC; RS[31:0] = v0

  // Notes on the sheet:
  //   中断源
  //   控制位
  //   中断等待指示
  //   暂停节拍，不能为0
  //   戳工具置1进入计数暂停模式，ctrl+k时钟自动运行到对应节拍暂停
  //   ctrl+k关闭时钟连续运行，将控制位置零，进入单步调试模式调试
  //   用这个时钟源需要去掉电路中的其他时钟源
  //   数码管输出
  //   可计数暂停的时钟源
  //   contents of rom_1 (hex, n*v repeats v):
  //   20100000 20110000 20120000 20130000 36100000 36310001 36520002 36730003 ae100000 ae110004 ae120008
  //   ae13000c 2002000a 20110000 20120000 20130000 c
  //   OP
  //   rs
  //   rt
  //   JMP
  //   JR
  //   OP
  //   Func
  //   Beq
  //   Bne
  //   MemToReg
  //   MemWrite
  //   AluOP
  //   AluSrcB
  //   RegWrite
  //   JAL
  //   RegDst
  //   Syscall
  //   流水调试日志用
  //   为方便自动评测，需要输出流水线各段保存的PC值，注意是PC不是PC+4，另外ID段寄存器写入信息，Mem段内存写入信息也要输出
endmodule

// ID/EX
module \气泡流水线  (
  output RegWrite,
  output MemWrite,
  output [31:0] IF_PC,
  output [31:0] ID_PC,
  output [31:0] EX_PC,
  output [31:0] M_PC,
  output [31:0] WB_PC,
  output [31:0] RDin,
  output [31:0] MDin,
  output [31:0] LedData,
  output [31:0] Imm,
  output [31:0] v0,
  output [31:0] a0
);

  wire AluSrcB, and_1_out, and_2_out, Beq, BeqOut, Bne, BneOut, Branch, CLK, clock_1_out, comparator_1_eq,
       comparator_1_lt, comparator_2_eq, d_ff_1_q, DataRelate, equal, EX_MEM_jalout, EX_MEM_mem_halt,
       EX_MEM_mentoregout, EX_RegWrite, Go, Halt, HaltOut, ID_EX_alusrcbout, ID_EX_jalout, ID_EX_memtoregout,
       ID_EX_memwriteout, ID_MemWrite, ID_RegWrite, IR1, IR2, IR3, JAL, JMP, JMPOut, JR, JROut, MEM_RegWrite,
       MEM_WB_jalout, MEM_WB_mentoregout, MemToReg, multiplexer_2_out, multiplexer_3_out, multiplexer_9_out,
       nand_1_out, not_1_out, not_2_out, RegDst, RST, SignedExt, Syscall, SyscallOut, W1, W2, W3,
       \源寄存器使用情况_1_r1_used , \源寄存器使用情况_1_r2_used ;
  wire [3:0] AluOP, ID_EX_aluopout;
  wire [4:0] EX_WriteReg_num, ID_EX_shamtout, MEM_WB_w_out, MEM_WriteReg_num, multiplexer_6_out,
       multiplexer_7_out, R1_num, R2_num;
  wire [5:0] Func;
  wire [12:0] CNT_num;
  wire [15:0] \LoadUse次数 , \总周期数 , \插入气泡数 , \无条件分支数 , \条件分支成功数 ;
  wire [31:0] adder_1_out, adder_2_out, bit_extender_1_out, bit_extender_2_out, EX_MEM_aluout_2,
       ID_EX_immout, ID_EX_pcout, IF_ID_pc_4out, JAddr, MEM_WB_aluout_2, MEM_WB_menout, MEM_WB_pcout,
       mips_alu_1_result, mips_regifile_1_r1, mips_regifile_1_r2, multiplexer_1_out, multiplexer_8_out,
       multiplexer_10_out, multiplexer_11_out, multiplexer_12_out, multiplexer_14_out, PCToMem, ram_1_data,
       rom_1_data, shifter_1_out;
  wire [31:6] IR;

  Button \u_总复位  (.out(RST));
  Button _1 (.out(IR1));
  Button _2 (.out(IR2));
  Button _3 (.out(IR3));
  Button \u_继续运行  (.out(Go));
  LED #(.active("true")) led_1 (.in(W1));
  LED #(.active("true")) led_2 (.in(W2));
  LED #(.active("true")) led_3 (.in(W3));
  D_Flip_Flop #(.trigger("high"), .Pre_Clr_Positions("LEGACY"), .NegatePresetClear("false"), .enable("true"), .NewFFLayout("false")) d_ff_1 (.Q(d_ff_1_q));  // open: clk, D, Qn, preset, en, reset
  // Probe on 13'hc
  Hex_Digit_Display hex_digit_display_1 (.value(LedData[31:28]));  // open: dp
  Comparator #(.width(13), .mode("twosComplement")) comparator_1 (
    .a(CNT_num), .b(13'hc), .eq(comparator_1_eq), .lt(comparator_1_lt));  // open: gt
  Clock #(.highDuration(1), .lowDuration(1)) clock_1 (.out(clock_1_out));
  Hex_Digit_Display hex_digit_display_2 (.value(LedData[23:20]));  // open: dp
  Hex_Digit_Display hex_digit_display_3 (.value(LedData[27:24]));  // open: dp
  nand nand_1 (nand_1_out, d_ff_1_q, comparator_1_eq);
  Counter #(.width(13), .max('h1fff), .ongoal("stay"), .trigger("rising"), .behavior("old")) counter_1 (
    .count(comparator_1_lt), .Q(CNT_num), .clk(clock_1_out));  // open: load, D, carry, clr, preset
  Hex_Digit_Display hex_digit_display_4 (.value(LedData[15:12]));  // open: dp
  Hex_Digit_Display hex_digit_display_5 (.value(LedData[19:16]));  // open: dp
  \单周期硬布线控制器  \u_单周期硬布线控制器_1  (
    .Func(Func), .OP(IR[31:26]), .ALU_OP(AluOP), .MemToReg(MemToReg), .MemWrite(ID_MemWrite),
    .ALU_SRC(AluSrcB), .RegWrite(ID_RegWrite), .SysCALL(Syscall), .SignedExt(SignedExt), .RegDst(RegDst),
    .JR(JR), .JMP(JMP), .Beq(Beq), .JAL(JAL), .Bne(Bne));
  Hex_Digit_Display hex_digit_display_6 (.value(LedData[7:4]));  // open: dp
  Hex_Digit_Display hex_digit_display_7 (.value(LedData[11:8]));  // open: dp
  Clock #(.highDuration(1), .lowDuration(1)) clock_2 ();  // open: out
  assign CLK = nand_1_out ? clock_1_out : 1'bz;  // Controlled_Buffer controlled_buffer_1
  Pull_Resistor #(.pull(1)) pull_resistor_1 (.node(CLK));
  Hex_Digit_Display hex_digit_display_8 (.value(LedData[3:0]));  // open: dp
  // Probe on \总周期数 
  // Probe on \总周期数 
  // Probe on \无条件分支数 
  // Probe on \条件分支成功数 
  // Probe on \插入气泡数 
  // Probe on \LoadUse次数 
  // Probe on IF_PC[11:0]
  // Probe on EX_PC[11:0]
  // Probe on ID_PC[11:0]
  // Probe on M_PC[11:0]
  // Probe on WB_PC[11:0]
  Multiplexer #(.select(1), .width(32), .disabled("Z"), .enable("false")) multiplexer_1 (
    .in0(adder_1_out), .in1(multiplexer_10_out), .out(multiplexer_1_out), .sel(Branch));
  Register #(.width(32), .trigger("rising"), .Select("low")) PC (
    .D(multiplexer_1_out), .en(multiplexer_2_out), .Q(IF_PC), .clk(CLK));  // open: clr
  Multiplexer #(.select(1), .width(1), .disabled("Z"), .enable("false")) multiplexer_2 (
    .in0(not_1_out), .in1(1'b0), .out(multiplexer_2_out), .sel(DataRelate));
  not not_1 (not_1_out, HaltOut);
  Counter #(.width(16), .max('hffff), .ongoal("wrap"), .trigger("rising"), .behavior("old")) counter_2 (
    .count(not_1_out), .Q(\总周期数 ), .clk(CLK), .clr(RST));  // open: load, D, carry, preset
  \源寄存器使用情况  \u_源寄存器使用情况_1  (
    .OP0(IR[26]), .OP1(IR[27]), .OP2(IR[28]), .OP3(IR[29]), .OP4(IR[30]), .OP5(IR[31]), .F0(Func[0]),
    .F1(Func[1]), .F2(Func[2]), .F3(Func[3]), .F4(Func[4]), .F5(Func[5]), .R1_Used(\源寄存器使用情况_1_r1_used ),
    .R2_Used(\源寄存器使用情况_1_r2_used ));
  Adder #(.width(32)) adder_1 (.a(IF_PC), .b(32'h4), .out(adder_1_out));  // open: cin, cout
  ROM #(.addrWidth(10), .dataWidth(32), .Select("high")) rom_1 (.addr(IF_PC[11:2]), .data(rom_1_data));
  \数据相关检测  \u_数据相关检测_1  (
    .R1_Used(\源寄存器使用情况_1_r1_used ), .R1_num(R1_num), .EX_RegWrite(EX_RegWrite),
    .EX_Write_num(EX_WriteReg_num), .R2_num(R2_num), .MEM_RegWrite(MEM_RegWrite), .Relate_Out(DataRelate),
    .MEM_Write_num(MEM_WriteReg_num), .R2_Used(\源寄存器使用情况_1_r2_used ));
  or or_1 (Branch, multiplexer_3_out, JMPOut);
  IF_ID IF_ID (
    .PC_4(adder_1_out), .RD(rom_1_data), .JAddr(IF_PC), .CLK(CLK), .PC_4Out(IF_ID_pc_4out),
    .RDOut({IR, Func}), .JAddrOut(ID_PC), .\同步清零_高电平有效 (Branch), .\使能端_低电平有效 (DataRelate));
  Multiplexer #(.select(1), .width(1), .disabled("Z"), .enable("false")) multiplexer_3 (
    .in0(BneOut), .in1(BeqOut), .out(multiplexer_3_out), .sel(equal));
  Multiplexer #(.select(1), .width(5), .disabled("Z"), .enable("false")) multiplexer_4 (
    .in0(IR[25:21]), .in1(5'b00010), .out(R1_num), .sel(Syscall));
  Multiplexer #(.select(1), .width(5), .disabled("Z"), .enable("false")) multiplexer_5 (
    .in0(IR[20:16]), .in1(5'b00100), .out(R2_num), .sel(Syscall));
  Multiplexer #(.select(1), .width(5), .disabled("Z"), .enable("false")) multiplexer_6 (
    .in0(IR[20:16]), .in1(IR[15:11]), .out(multiplexer_6_out), .sel(RegDst));
  assign bit_extender_1_out = {{16{1'b0}}, {IR[15:6], Func}};  // Bit_Extender bit_extender_1
  assign bit_extender_2_out = {{16{IR[15]}}, {IR[15:6], Func}};  // Bit_Extender bit_extender_2
  Multiplexer #(.select(1), .width(5), .disabled("Z"), .enable("false")) multiplexer_7 (
    .in0(multiplexer_6_out), .in1({5{1'b1}}), .out(multiplexer_7_out), .sel(JAL));
  MIPS_Regifile mips_regifile_1 (
    .Din(RDin), .Clk(CLK), .R1(mips_regifile_1_r1), .R2(mips_regifile_1_r2), .WE(RegWrite),
    .W_num(MEM_WB_w_out), .R1_num(R1_num), .R2_num(R2_num));
  Multiplexer #(.select(1), .width(32), .disabled("Z"), .enable("false")) multiplexer_8 (
    .in0(bit_extender_1_out), .in1(bit_extender_2_out), .out(multiplexer_8_out), .sel(SignedExt));
  Multiplexer #(.select(1), .width(1), .disabled("Z"), .enable("false")) multiplexer_9 (
    .in0(Branch), .in1(1'b1), .out(multiplexer_9_out), .sel(DataRelate));
  ID_EX ID_EX (
    .RegWrite(ID_RegWrite), .AluOP(AluOP), .MemToReg(MemToReg), .AluSrcB(AluSrcB), .PC(IF_ID_pc_4out),
    .A(mips_regifile_1_r1), .B(mips_regifile_1_r2), .Imm(multiplexer_8_out), .Shamt(IR[10:6]),
    .W_num(multiplexer_7_out), .MemWrite(ID_MemWrite), .JMP(JMP), .Beq(Beq), .Bne(Bne), .CLK(CLK),
    .RegWriteOut(EX_RegWrite), .AluOPOut(ID_EX_aluopout), .MemToRegOut(ID_EX_memtoregout),
    .AluSrcBOut(ID_EX_alusrcbout), .PCOut(ID_EX_pcout), .AOut(Imm), .BOut(a0), .ImmOut(ID_EX_immout),
    .ShamtOut(ID_EX_shamtout), .W_Out(EX_WriteReg_num), .MemWriteOut(ID_EX_memwriteout), .JMPOut(JMPOut),
    .BeqOut(BeqOut), .BneOut(BneOut), .\同步清零_高电平有效 (multiplexer_9_out),
    .JAddr({ID_PC[31:28], IR[25:6], Func, 2'b00}), .JAddr_2(JAddr), .JR(JR), .JROut(JROut), .JAL(JAL),
    .JALOut(ID_EX_jalout), .Syscall(Syscall), .EX_SysCall(SyscallOut), .ID_PC(ID_PC), .EX_PC(EX_PC));  // open: 使能端_低电平有效, Op, OpOut, DataRedirect, DataDirectOut
  Multiplexer #(.select(1), .width(32), .disabled("Z"), .enable("false")) multiplexer_10 (
    .in0(adder_2_out), .in1(multiplexer_11_out), .out(multiplexer_10_out), .sel(JMPOut));
  Multiplexer #(.select(1), .width(32), .disabled("Z"), .enable("false")) multiplexer_11 (
    .in0(JAddr), .in1(Imm), .out(multiplexer_11_out), .sel(JROut));
  Adder #(.width(32)) adder_2 (.a(ID_EX_pcout), .b(shifter_1_out), .out(adder_2_out));  // open: cin, cout
  Shifter #(.width(32), .shift("ll")) shifter_1 (.in(ID_EX_immout), .\dist (5'b00010), .out(shifter_1_out));
  Multiplexer #(.select(1), .width(32), .disabled("Z"), .enable("false")) multiplexer_12 (
    .in0(a0), .in1(ID_EX_immout), .out(multiplexer_12_out), .sel(ID_EX_alusrcbout));
  MIPS_ALU mips_alu_1 (
    .X(Imm), .Y(multiplexer_12_out), .AluOP(ID_EX_aluopout), .Equal(equal), .Result(mips_alu_1_result),
    .shamt(ID_EX_shamtout));  // open: Result_2
  Comparator #(.width(32), .mode("twosComplement")) comparator_2 (
    .a(Imm), .b(32'h32), .eq(comparator_2_eq));  // open: gt, lt
  not not_2 (not_2_out, comparator_2_eq);
  EX_MEM EX_MEM (
    .RegWrite(EX_RegWrite), .MenToReg(ID_EX_memtoregout), .AluOut(mips_alu_1_result), .B(a0),
    .W_num(EX_WriteReg_num), .MemWrite(ID_EX_memwriteout), .CLK(CLK), .RegWriteOut(MEM_RegWrite),
    .MenToRegOut(EX_MEM_mentoregout), .AluOut_2(EX_MEM_aluout_2), .BOut(MDin), .W_Out(MEM_WriteReg_num),
    .MemWriteOut(MemWrite), .JAL(ID_EX_jalout), .JALOut(EX_MEM_jalout), .PC_4(ID_EX_pcout), .PCOut(PCToMem),
    .EX_Halt(Halt), .MEM_Halt(EX_MEM_mem_halt), .EX_PC(EX_PC), .MEM_PC(M_PC));  // open: 同步清零_高电平有效, 使能端_低电平有效, Op, OpOut
  and and_1 (and_1_out, not_2_out, SyscallOut);
  Register #(.width(1), .trigger("rising"), .Select("low")) register_1 (
    .D(and_2_out), .en(and_2_out), .Q(Halt), .clk(CLK), .clr(Go));
  and and_2 (and_2_out, SyscallOut, comparator_2_eq);
  Register #(.width(32), .trigger("rising"), .Select("low")) register_2 (
    .D(a0), .en(and_1_out), .Q(LedData), .clk(CLK));  // open: clr
  RAM #(.addrWidth(10), .dataWidth(32), .bus("separate"), .Select("high")) ram_1 (
    .addr(EX_MEM_aluout_2[11:2]), .din(MDin), .data(ram_1_data), .str(MemWrite), .clk(CLK));  // open: sel, ld, clr
  MEM_WB MEM_WB (
    .RegWrite(MEM_RegWrite), .MenToReg(EX_MEM_mentoregout), .MemOut(ram_1_data), .AluOut(EX_MEM_aluout_2),
    .W_num(MEM_WriteReg_num), .CLK(CLK), .RegWriteOut(RegWrite), .MenToRegOut(MEM_WB_mentoregout),
    .MenOut(MEM_WB_menout), .AluOut_2(MEM_WB_aluout_2), .W_Out(MEM_WB_w_out), .JAL(EX_MEM_jalout),
    .JALOut(MEM_WB_jalout), .PC_4(PCToMem), .PCOut(MEM_WB_pcout), .MEM_Halt(EX_MEM_mem_halt),
    .WB_Halt(HaltOut), .MEM_PC(M_PC), .WB_PC(WB_PC));  // open: 同步清零_高电平有效, 使能端_低电平有效, Op, OpOut
  Multiplexer #(.select(1), .width(32), .disabled("Z"), .enable("false")) multiplexer_13 (
    .in0(multiplexer_14_out), .in1(MEM_WB_pcout), .out(RDin), .sel(MEM_WB_jalout));
  Multiplexer #(.select(1), .width(32), .disabled("Z"), .enable("false")) multiplexer_14 (
    .in0(MEM_WB_aluout_2), .in1(MEM_WB_menout), .out(multiplexer_14_out), .sel(MEM_WB_mentoregout));

  assign v0 = Imm;

  // Other names for the same wires on the sheet: IR[5:0] = Func; shamt[4:0] = IR[10:6]; rd[4:0] = IR[15:11];
  //   rt[4:0] = IR[20:16]; rs_t[4:0] = IR[25:21]; EX_R2[31:0] = a0; OP[5:0] = IR[31:26]; MEM_PC[31:0] = M_PC;
  //   PC[31:0] = IF_PC; EX_R1[31:0] = Imm; ImmOut[31:0] = Imm; RS[31:0] = Imm

  // Notes on the sheet:
  //   中断源
  //   中断等待指示
  //   控制位
  //   暂停节拍，不能为0
  //   数码管输出应该用寄存器锁存，否则显示数据只能一闪而过
  //   戳工具置1进入计数暂停模式，ctrl+k时钟自动运行到对应节拍暂停
  //   ctrl+k关闭时钟连续运行，将控制位置零，进入单步调试模式调试
  //   JMP
  //   JR
  //   OP
  //   Func
  //   数码管输出
  //   可计数暂停的时钟源
  //   Beq
  //   Bne
  //   MemToReg
  //   MemWrite
  //   AluOP
  //   AluSrcB
  //   RegWrite
  //   JAL
  //   RegDst
  //   Syscall
  //   流水调试日志用
  //   contents of rom_1 (hex, n*v repeats v):
  //   20110001 8000c05 20110001 20120002 20130003 8000c09 20110001 20120002 20130003 8000c0d 20110001
  //   20120002 20130003 8000c11 20110001 20120002 20130003 c000cb8 20100001 20110001 118fc0 112020
  //   20020022 c 118882 12200001 8000c15 112020 20020022 c 20110001 118880 112020 20020022 c 12200001
  //   8000c1f 20110001 118fc0 112020 20020022 c 1188c3 112020 20020022 c 118903 112020 20020022 c 118903
  //   112020 20020022 c 118903 112020 20020022 c 118903 112020 20020022 c 118903 112020 20020022 c 118903
  //   112020 20020022 c 118903 112020 20020022 c 20100001 109fc0 139fc3 8021 2012000c 24160003 26100001
  //   3210000f 20080008 20090001 139900 2709825 132020 20020022 c 1094022 1500fff9 22100001 2018000f
  //   2188024 108700 20080008 20090001 139902 2709825 132021 20020022 c 1094022 1500fff9 108702 2c9b022
  //   12c00001 8000c50 4020 1084027 84400 3508ffff 82021 20020022 c 2010ffff 20110000 ae300000 22100001
  //   22310004 ae300000 22100001 22310004 ae300000 22100001 22310004 ae300000 22100001 22310004 ae300000
  //   22100001 22310004 ae300000 22100001 22310004 ae300000 22100001 22310004 ae300000 22100001 22310004
  //   ae300000 22100001 22310004 ae300000 22100001 22310004 ae300000 22100001 22310004 ae300000 22100001
  //   22310004 ae300000 22100001 22310004 ae300000 22100001 22310004 ae300000 22100001 22310004 ae300000
  //   22100001 22310004 22100001 8020 2011003c 8e130000 8e340000 274402a 11000002 ae330000 ae140000
  //   2231fffc 1611fff8 102020 20020022 c 22100004 2011003c 1611fff2 20020032 c 20100000 22100001 102020
  //   20020022 c 22100002 102020 20020022 c 22100003 102020 20020022 c 22100004 102020 20020022 c 22100005
  //   102020 20020022 c 22100006 102020 20020022 c 22100007 102020 20020022 c 22100008 102020 20020022
  //   20020022 c 3e00008
  //   OP
  //   rs
  //   rt
  //   为方便自动评测，需要输出流水线各段保存的PC值，注意是PC不是PC+4，另外ID段寄存器写入信息，Mem段内存写入信息也要输出
endmodule

module \重定向流水线  (
  output RegWrite,
  output MemWrite,
  output [31:0] IF_PC,
  output [31:0] ID_PC,
  output [31:0] EX_PC,
  output [31:0] M_PC,
  output [31:0] WB_PC,
  output [31:0] RDin,
  output [31:0] MDin,
  output [31:0] LedData,
  output [31:0] v0,
  output [31:0] a0
);

  wire AluSrcB, and_1_out, and_2_out, and_3_out, Beq, BeqOut, Bne, BneOut, Branch, CLK, comparator_1_eq,
       comparator_2_eq, equal, EX_AluSrcB, EX_MEM_jalout, EX_MEM_mem_halt, EX_MEM_mentoregout, EX_RegWrite,
       Go, Halt, HaltOut, ID_EX_jalout, ID_EX_memtoregout, ID_EX_memwriteout, ID_MemWrite, ID_RegWrite, IR1,
       IR2, IR3, JAL, JMP, JMPOut, JR, JROut, MEM_RegWrite, MEM_WB_jalout, MEM_WB_mentoregout, MemToReg,
       multiplexer_2_out, multiplexer_9_out, not_1_out, not_2_out, not_3_out, RegDst, RST, SignedExt, stall,
       Syscall, SyscallOut, W1, W2, W3, \条件分支成功跳转 , \源寄存器使用情况_1_r1_used , \源寄存器使用情况_1_r2_used ;
  wire [3:0] AluOP, ID_EX_aluopout;
  wire [4:0] EX_Forward, EX_WriteReg_num, Forward, ID_EX_shamtout, MEM_WB_w_out, MEM_WriteReg_num,
       multiplexer_6_out, multiplexer_7_out, R1_num, R2_num;
  wire [5:0] EX_Op, Func, MEM_Op;
  wire [15:0] \LoadUse次数 , \总周期数 , \无条件分支数 , \条件分支成功数 ;
  wire [31:0] adder_1_out, adder_2_out, bit_extender_1_out, bit_extender_2_out, EX_Imm, EX_R2, ID_EX_aout,
       ID_EX_pcout, IF_ID_pc_4out, JAddr, MEM_AluRes, MEM_WB_pcout, mips_alu_1_result, mips_regifile_1_r1,
       mips_regifile_1_r2, multiplexer_1_out, multiplexer_8_out, multiplexer_10_out, multiplexer_11_out,
       multiplexer_12_out, multiplexer_13_out, multiplexer_16_out, multiplexer_18_out, PCToMem, ram_1_data,
       rom_1_data, shifter_1_out, WB_AluRes, WB_MEMRes;
  wire [31:6] IR;

  Clock #(.highDuration(1), .lowDuration(1)) clock_1 (.out(CLK));
  Button _1 (.out(IR1));
  Button _2 (.out(IR2));
  Button _3 (.out(IR3));
  Button \u_继续运行  (.out(Go));
  LED #(.active("true")) led_1 (.in(W1));
  LED #(.active("true")) led_2 (.in(W2));
  LED #(.active("true")) led_3 (.in(W3));
  Hex_Digit_Display hex_digit_display_1 (.value(LedData[31:28]));  // open: dp
  not not_1 (not_1_out, HaltOut);
  and and_1 (and_1_out, not_1_out, stall);
  Hex_Digit_Display hex_digit_display_2 (.value(LedData[23:20]));  // open: dp
  Hex_Digit_Display hex_digit_display_3 (.value(LedData[27:24]));  // open: dp
  // Probe on \LoadUse次数 
  Counter #(.width(16), .max('hffff), .ongoal("wrap"), .trigger("rising"), .behavior("old")) counter_1 (
    .count(and_1_out), .Q(\LoadUse次数 ), .clk(CLK), .clr(RST));  // open: load, D, carry, preset
  \单周期硬布线控制器  \u_单周期硬布线控制器_1  (
    .Func(Func), .OP(IR[31:26]), .ALU_OP(AluOP), .MemToReg(MemToReg), .MemWrite(ID_MemWrite),
    .ALU_SRC(AluSrcB), .RegWrite(ID_RegWrite), .SysCALL(Syscall), .SignedExt(SignedExt), .RegDst(RegDst),
    .JR(JR), .JMP(JMP), .Beq(Beq), .JAL(JAL), .Bne(Bne));
  Comparator #(.width(32), .mode("twosComplement")) comparator_1 (
    .a(v0), .b(32'h32), .eq(comparator_1_eq));  // open: gt, lt
  Hex_Digit_Display hex_digit_display_4 (.value(LedData[15:12]));  // open: dp
  Hex_Digit_Display hex_digit_display_5 (.value(LedData[19:16]));  // open: dp
  not not_2 (not_2_out, comparator_1_eq);
  and and_2 (and_2_out, not_2_out, SyscallOut);
  and and_3 (and_3_out, SyscallOut, comparator_1_eq);
  Hex_Digit_Display hex_digit_display_6 (.value(LedData[7:4]));  // open: dp
  Hex_Digit_Display hex_digit_display_7 (.value(LedData[11:8]));  // open: dp
  // Probe on \总周期数 
  Register #(.width(32), .trigger("rising"), .Select("low")) register_1 (
    .D(a0), .en(and_2_out), .Q(LedData), .clk(CLK));  // open: clr
  Register #(.width(1), .trigger("rising"), .Select("low")) register_2 (
    .D(and_3_out), .en(and_3_out), .Q(Halt), .clk(CLK), .clr(Go));
  Hex_Digit_Display hex_digit_display_8 (.value(LedData[3:0]));  // open: dp
  Counter #(.width(16), .max('hffff), .ongoal("wrap"), .trigger("rising"), .behavior("old")) counter_2 (
    .count(JMPOut), .Q(\无条件分支数 ), .clk(CLK), .clr(RST));  // open: load, D, carry, preset
  // Probe on \总周期数 
  // Probe on \无条件分支数 
  // Probe on \总周期数 
  // Probe on \无条件分支数 
  // Probe on \条件分支成功数 
  // Probe on \LoadUse次数 
  // Probe on \LoadUse次数 
  Button button_1 (.out(RST));
  // Probe on IF_PC[11:0]
  // Probe on ID_PC[11:0]
  // Probe on EX_PC[11:0]
  // Probe on M_PC[11:0]
  // Probe on \条件分支成功数 
  Counter #(.width(16), .max('hffff), .ongoal("wrap"), .trigger("rising"), .behavior("old")) counter_3 (
    .count(\条件分支成功跳转 ), .Q(\条件分支成功数 ), .clk(CLK), .clr(RST));  // open: load, D, carry, preset
  // Probe on WB_PC[11:0]
  Multiplexer #(.select(1), .width(32), .disabled("Z"), .enable("false")) multiplexer_1 (
    .in0(adder_1_out), .in1(multiplexer_10_out), .out(multiplexer_1_out), .sel(Branch));
  Multiplexer #(.select(1), .width(1), .disabled("Z"), .enable("false")) multiplexer_2 (
    .in0(not_3_out), .in1(1'b0), .out(multiplexer_2_out), .sel(stall));
  not not_3 (not_3_out, HaltOut);
  Comparator #(.width(6), .mode("twosComplement")) comparator_2 (
    .a(IR[31:26]), .b(6'b100011), .eq(comparator_2_eq));  // open: gt, lt
  Register #(.width(32), .trigger("rising"), .Select("low")) PC (
    .D(multiplexer_1_out), .en(multiplexer_2_out), .Q(IF_PC), .clk(CLK));  // open: clr
  Counter #(.width(16), .max('hffff), .ongoal("wrap"), .trigger("rising"), .behavior("old")) counter_4 (
    .count(not_3_out), .Q(\总周期数 ), .clk(CLK), .clr(RST));  // open: load, D, carry, preset
  or or_1 (Forward[4], comparator_2_eq, 1'b0);
  Adder #(.width(32)) adder_1 (.a(IF_PC), .b(32'h4), .out(adder_1_out));  // open: cin, cout
  ROM #(.addrWidth(10), .dataWidth(32), .Select("high")) rom_1 (.addr(IF_PC[11:2]), .data(rom_1_data));
  IF_ID IF_ID (
    .PC_4(adder_1_out), .RD(rom_1_data), .JAddr(IF_PC), .CLK(CLK), .PC_4Out(IF_ID_pc_4out),
    .RDOut({IR, Func}), .JAddrOut(ID_PC), .\同步清零_高电平有效 (Branch), .\使能端_低电平有效 (stall));
  Multiplexer #(.select(1), .width(1), .disabled("Z"), .enable("false")) multiplexer_3 (
    .in0(BneOut), .in1(BeqOut), .out(\条件分支成功跳转 ), .sel(equal));
  or or_2 (Branch, \条件分支成功跳转 , JMPOut);
  \源寄存器使用情况  \u_源寄存器使用情况_1  (
    .OP0(IR[26]), .OP1(IR[27]), .OP2(IR[28]), .OP3(IR[29]), .OP4(IR[30]), .OP5(IR[31]), .F0(Func[0]),
    .F1(Func[1]), .F2(Func[2]), .F3(Func[3]), .F4(Func[4]), .F5(Func[5]), .R1_Used(\源寄存器使用情况_1_r1_used ),
    .R2_Used(\源寄存器使用情况_1_r2_used ));
  Multiplexer #(.select(1), .width(5), .disabled("Z"), .enable("false")) multiplexer_4 (
    .in0(IR[25:21]), .in1(5'b00010), .out(R1_num), .sel(Syscall));
  Multiplexer #(.select(1), .width(5), .disabled("Z"), .enable("false")) multiplexer_5 (
    .in0(IR[20:16]), .in1(5'b00100), .out(R2_num), .sel(Syscall));
  Multiplexer #(.select(1), .width(5), .disabled("Z"), .enable("false")) multiplexer_6 (
    .in0(IR[20:16]), .in1(IR[15:11]), .out(multiplexer_6_out), .sel(RegDst));
  assign bit_extender_1_out = {{16{1'b0}}, {IR[15:6], Func}};  // Bit_Extender bit_extender_1
  assign bit_extender_2_out = {{16{IR[15]}}, {IR[15:6], Func}};  // Bit_Extender bit_extender_2
  Multiplexer #(.select(1), .width(5), .disabled("Z"), .enable("false")) multiplexer_7 (
    .in0(multiplexer_6_out), .in1({5{1'b1}}), .out(multiplexer_7_out), .sel(JAL));
  \数据重定向检测  \u_数据重定向检测  (
    .R1_Used(\源寄存器使用情况_1_r1_used ), .R1_num(R1_num), .EX_Write_num(EX_WriteReg_num),
    .MEM_Write_num(MEM_WriteReg_num), .R2_num(R2_num), .R2_Used(\源寄存器使用情况_1_r2_used ), .R1MEN(Forward[0]),
    .R1WB(Forward[1]), .R2MEN(Forward[2]), .R2WB(Forward[3]), .MEM_RegWrite(MEM_RegWrite),
    .EX_RegWrite(EX_RegWrite));
  \load_use检测  LoadUse (
    .R1_Used(\源寄存器使用情况_1_r1_used ), .EX_LW(EX_Forward[4]), .R1_num(R1_num), .EX_Write_num(EX_WriteReg_num),
    .R2_num(R2_num), .R2_Used(\源寄存器使用情况_1_r2_used ), .stall(stall));
  MIPS_Regifile mips_regifile_1 (
    .Din(RDin), .Clk(CLK), .R1(mips_regifile_1_r1), .R2(mips_regifile_1_r2), .WE(RegWrite),
    .W_num(MEM_WB_w_out), .R1_num(R1_num), .R2_num(R2_num));
  Multiplexer #(.select(1), .width(32), .disabled("Z"), .enable("false")) multiplexer_8 (
    .in0(bit_extender_1_out), .in1(bit_extender_2_out), .out(multiplexer_8_out), .sel(SignedExt));
  Multiplexer #(.select(1), .width(1), .disabled("Z"), .enable("false")) multiplexer_9 (
    .in0(Branch), .in1(1'b1), .out(multiplexer_9_out), .sel(stall));
  ID_EX ID_EX (
    .RegWrite(ID_RegWrite), .AluOP(AluOP), .MemToReg(MemToReg), .AluSrcB(AluSrcB), .PC(IF_ID_pc_4out),
    .A(mips_regifile_1_r1), .B(mips_regifile_1_r2), .Imm(multiplexer_8_out), .Shamt(IR[10:6]),
    .W_num(multiplexer_7_out), .MemWrite(ID_MemWrite), .JMP(JMP), .Beq(Beq), .Bne(Bne), .CLK(CLK),
    .RegWriteOut(EX_RegWrite), .AluOPOut(ID_EX_aluopout), .MemToRegOut(ID_EX_memtoregout),
    .AluSrcBOut(EX_AluSrcB), .PCOut(ID_EX_pcout), .AOut(ID_EX_aout), .BOut(EX_R2), .ImmOut(EX_Imm),
    .ShamtOut(ID_EX_shamtout), .W_Out(EX_WriteReg_num), .MemWriteOut(ID_EX_memwriteout), .JMPOut(JMPOut),
    .BeqOut(BeqOut), .BneOut(BneOut), .\同步清零_高电平有效 (multiplexer_9_out), .\使能端_低电平有效 (HaltOut),
    .JAddr({ID_PC[31:28], IR[25:6], Func, 2'b00}), .JAddr_2(JAddr), .JR(JR), .JROut(JROut), .JAL(JAL),
    .JALOut(ID_EX_jalout), .Syscall(Syscall), .EX_SysCall(SyscallOut), .Op(IR[31:26]), .OpOut(EX_Op),
    .DataRedirect(Forward), .DataDirectOut(EX_Forward), .ID_PC(ID_PC), .EX_PC(EX_PC));
  Multiplexer #(.select(1), .width(32), .disabled("Z"), .enable("false")) multiplexer_10 (
    .in0(adder_2_out), .in1(multiplexer_11_out), .out(multiplexer_10_out), .sel(JMPOut));
  Multiplexer #(.select(1), .width(32), .disabled("Z"), .enable("false")) multiplexer_11 (
    .in0(JAddr), .in1(v0), .out(multiplexer_11_out), .sel(JROut));
  Multiplexer #(.select(1), .width(32), .disabled("Z"), .enable("false")) multiplexer_12 (
    .in0(EX_R2), .in1(RDin), .out(multiplexer_12_out), .sel(EX_Forward[3]));
  Multiplexer #(.select(1), .width(32), .disabled("Z"), .enable("false")) multiplexer_13 (
    .in0(ID_EX_aout), .in1(RDin), .out(multiplexer_13_out), .sel(EX_Forward[1]));
  Multiplexer #(.select(1), .width(32), .disabled("Z"), .enable("false")) multiplexer_14 (
    .in0(multiplexer_12_out), .in1(MEM_AluRes), .out(a0), .sel(EX_Forward[2]));
  Multiplexer #(.select(1), .width(32), .disabled("Z"), .enable("false")) multiplexer_15 (
    .in0(multiplexer_13_out), .in1(MEM_AluRes), .out(v0), .sel(EX_Forward[0]));
  Adder #(.width(32)) adder_2 (.a(ID_EX_pcout), .b(shifter_1_out), .out(adder_2_out));  // open: cin, cout
  Shifter #(.width(32), .shift("ll")) shifter_1 (.in(EX_Imm), .\dist (5'b00010), .out(shifter_1_out));
  Multiplexer #(.select(1), .width(32), .disabled("Z"), .enable("false")) multiplexer_16 (
    .in0(a0), .in1(EX_Imm), .out(multiplexer_16_out), .sel(EX_AluSrcB));
  MIPS_ALU mips_alu_1 (
    .X(v0), .Y(multiplexer_16_out), .AluOP(ID_EX_aluopout), .Equal(equal), .Result(mips_alu_1_result),
    .shamt(ID_EX_shamtout));  // open: Result_2
  EX_MEM EX_MEM (
    .RegWrite(EX_RegWrite), .MenToReg(ID_EX_memtoregout), .AluOut(mips_alu_1_result), .B(a0),
    .W_num(EX_WriteReg_num), .MemWrite(ID_EX_memwriteout), .CLK(CLK), .RegWriteOut(MEM_RegWrite),
    .MenToRegOut(EX_MEM_mentoregout), .AluOut_2(MEM_AluRes), .BOut(MDin), .W_Out(MEM_WriteReg_num),
    .MemWriteOut(MemWrite), .\使能端_低电平有效 (HaltOut), .JAL(ID_EX_jalout), .JALOut(EX_MEM_jalout),
    .PC_4(ID_EX_pcout), .PCOut(PCToMem), .EX_Halt(Halt), .MEM_Halt(EX_MEM_mem_halt), .Op(EX_Op),
    .OpOut(MEM_Op), .EX_PC(EX_PC), .MEM_PC(M_PC));  // open: 同步清零_高电平有效
  RAM #(.addrWidth(10), .dataWidth(32), .bus("separate"), .Select("high")) ram_1 (
    .addr(MEM_AluRes[11:2]), .din(MDin), .data(ram_1_data), .str(MemWrite), .clk(CLK));  // open: sel, ld, clr
  MEM_WB MEM_WB (
    .RegWrite(MEM_RegWrite), .MenToReg(EX_MEM_mentoregout), .MemOut(ram_1_data), .AluOut(MEM_AluRes),
    .W_num(MEM_WriteReg_num), .CLK(CLK), .RegWriteOut(RegWrite), .MenToRegOut(MEM_WB_mentoregout),
    .MenOut(WB_MEMRes), .AluOut_2(WB_AluRes), .W_Out(MEM_WB_w_out), .JAL(EX_MEM_jalout),
    .JALOut(MEM_WB_jalout), .PC_4(PCToMem), .PCOut(MEM_WB_pcout), .MEM_Halt(EX_MEM_mem_halt),
    .WB_Halt(HaltOut), .Op(MEM_Op), .MEM_PC(M_PC), .WB_PC(WB_PC));  // open: 同步清零_高电平有效, 使能端_低电平有效, OpOut
  Multiplexer #(.select(1), .width(32), .disabled("Z"), .enable("false")) multiplexer_17 (
    .in0(multiplexer_18_out), .in1(MEM_WB_pcout), .out(RDin), .sel(MEM_WB_jalout));
  Multiplexer #(.select(1), .width(32), .disabled("Z"), .enable("false")) multiplexer_18 (
    .in0(WB_AluRes), .in1(WB_MEMRes), .out(multiplexer_18_out), .sel(MEM_WB_mentoregout));

  // Other names for the same wires on the sheet: IR[5:0] = Func; shamt[4:0] = IR[10:6]; rd[4:0] = IR[15:11];
  //   rt[4:0] = IR[20:16]; rs_t[4:0] = IR[25:21]; EX_R1MEM = EX_Forward[0]; EX_R1WB = EX_Forward[1];
  //   EX_R2MEM = EX_Forward[2]; EX_R2WB = EX_Forward[3]; EX_Load = EX_Forward[4]; R1MEM = Forward[0];
  //   R1WB = Forward[1]; R2MEM = Forward[2]; R2WB = Forward[3]; ID_Load = Forward[4]; OP[5:0] = IR[31:26];
  //   MEM_PC[31:0] = M_PC; PC[31:0] = IF_PC; RS[31:0] = v0; 插入气泡数[15:0] = \LoadUse次数 

  // Notes on the sheet:
  //   中断源
  //   中断等待指示
  //   总复位信号应将除ROM以外所有存储组件全部清零
  //   JMP
  //   JR
  //   OP
  //   Func
  //   Beq
  //   Bne
  //   MemToReg
  //   MemWrite
  //   AluOP
  //   AluSrcB
  //   RegWrite
  //   JAL
  //   RegDst
  //   Syscall
  //   数码管输出
  //   数码管输出应该用寄存器锁存，否则显示数据只能一闪而过
  //   流水调试日志用
  //   contents of rom_1 (hex, n*v repeats v):
  //   20110001 8000c05 20110001 20120002 20130003 8000c09 20110001 20120002 20130003 8000c0d 20110001
  //   20120002 20130003 8000c11 20110001 20120002 20130003 c000cb8 20100001 20110001 118fc0 112020
  //   20020022 c 118882 12200001 8000c15 112020 20020022 c 20110001 118880 112020 20020022 c 12200001
  //   8000c1f 20110001 118fc0 112020 20020022 c 1188c3 112020 20020022 c 118903 112020 20020022 c 118903
  //   112020 20020022 c 118903 112020 20020022 c 118903 112020 20020022 c 118903 112020 20020022 c 118903
  //   112020 20020022 c 118903 112020 20020022 c 20100001 109fc0 139fc3 8021 2012000c 24160003 26100001
  //   3210000f 20080008 20090001 139900 2709825 132020 20020022 c 1094022 1500fff9 22100001 2018000f
  //   2188024 108700 20080008 20090001 139902 2709825 132021 20020022 c 1094022 1500fff9 108702 2c9b022
  //   12c00001 8000c50 4020 1084027 84400 3508ffff 82021 20020022 c 2010ffff 20110000 ae300000 22100001
  //   22310004 ae300000 22100001 22310004 ae300000 22100001 22310004 ae300000 22100001 22310004 ae300000
  //   22100001 22310004 ae300000 22100001 22310004 ae300000 22100001 22310004 ae300000 22100001 22310004
  //   ae300000 22100001 22310004 ae300000 22100001 22310004 ae300000 22100001 22310004 ae300000 22100001
  //   22310004 ae300000 22100001 22310004 ae300000 22100001 22310004 ae300000 22100001 22310004 ae300000
  //   22100001 22310004 22100001 8020 2011003c 8e130000 8e340000 274402a 11000002 ae330000 ae140000
  //   2231fffc 1611fff8 102020 20020022 c 22100004 2011003c 1611fff2 20020032 c 20100000 22100001 102020
  //   20020022 c 22100002 102020 20020022 c 22100003 102020 20020022 c 22100004 102020 20020022 c 22100005
  //   102020 20020022 c 22100006 102020 20020022 c 22100007 102020 20020022 c 22100008 102020 20020022
  //   20020022 c 3e00008
  //   为方便自动评测，需要输出流水线各段保存的PC值，注意是PC不是PC+4，另外ID段寄存器写入信息，Mem段内存写入信息也要输出
  //   OP
  //   rs
  //   rt
endmodule

module \中断按键参考电路  (
  input  \同步清零信号 ,
  output \与中断屏蔽位与 
);

  wire \_1号中断_out , and_1_out, clock_1_out, d_ff_1_q, or_1_out, or_2_out;

  Clock #(.highDuration(1), .lowDuration(1)) clock_1 (.out(clock_1_out));
  Button \_1号中断  (.out(\_1号中断_out ));
  or or_1 (or_1_out, \与中断屏蔽位与 , d_ff_1_q);
  LED #(.active("true")) \_1号中断等待指示灯  (.in(or_1_out));
  D_Flip_Flop #(.trigger("rising"), .Pre_Clr_Positions("LEGACY"), .NegatePresetClear("false"), .enable("true"), .NewFFLayout("false")) d_ff_1 (
    .clk(\_1号中断_out ), .D(1'b1), .Q(d_ff_1_q), .reset(\与中断屏蔽位与 ));  // open: Qn, preset, en
  or or_2 (or_2_out, d_ff_1_q, \与中断屏蔽位与 );
  and and_1 (and_1_out, or_2_out, ~\同步清零信号 );  // AND_Gate
  D_Flip_Flop #(.trigger("rising"), .Pre_Clr_Positions("LEGACY"), .NegatePresetClear("false"), .enable("true"), .NewFFLayout("false")) IR1 (
    .clk(clock_1_out), .D(and_1_out), .Q(\与中断屏蔽位与 ));  // open: Qn, preset, en, reset

  // Notes on the sheet:
  //   中断信号采样参考电路
  //   Reset 
endmodule

module \_32位流水  (
  input  [31:0] Din32,
  input  CLK,
  input  \同步清零_气泡_高电平有效 ,
  input  \使能端_低电平有效_stall_高电平有效 ,
  output [31:0] Dout32
);

  wire not_1_out;
  wire [31:0] multiplexer_1_out;

  Multiplexer #(.select(1), .width(32), .disabled("Z"), .enable("false")) multiplexer_1 (
    .in0(Din32), .in1({32{1'b0}}), .out(multiplexer_1_out), .sel(\同步清零_气泡_高电平有效 ));
  Pull_Resistor #(.pull(0)) pull_resistor_1 (.node(\同步清零_气泡_高电平有效 ));
  not not_1 (not_1_out, \使能端_低电平有效_stall_高电平有效 );
  Register #(.width(32), .trigger("rising"), .Select("low")) register_1 (
    .D(multiplexer_1_out), .en(not_1_out), .Q(Dout32), .clk(CLK));  // open: clr
  Pull_Resistor #(.pull(0)) pull_resistor_2 (.node(not_1_out));
endmodule

module \_1位流水接口  (
  input  Din1,
  input  CLK,
  input  \同步清零_气泡_高电平有效 ,
  input  \使能端_低电平有效_stall_高电平有效 ,
  output Dout1
);

  wire multiplexer_1_out, not_1_out;

  Multiplexer #(.select(1), .width(1), .disabled("Z"), .enable("false")) multiplexer_1 (
    .in0(Din1), .in1(1'b0), .out(multiplexer_1_out), .sel(\同步清零_气泡_高电平有效 ));
  Pull_Resistor #(.pull(0)) pull_resistor_1 (.node(\同步清零_气泡_高电平有效 ));
  not not_1 (not_1_out, \使能端_低电平有效_stall_高电平有效 );
  Register #(.width(1), .trigger("rising"), .Select("low")) register_1 (
    .D(multiplexer_1_out), .en(not_1_out), .Q(Dout1), .clk(CLK));  // open: clr
  Pull_Resistor #(.pull(0)) pull_resistor_2 (.node(not_1_out));
endmodule

module \_4位  (
  input  [3:0] Din1,
  input  CLK,
  input  \同步清零_气泡_高电平有效 ,
  input  \使能端_低电平有效_stall_高电平有效 ,
  output [3:0] Dout1
);

  wire not_1_out;
  wire [3:0] multiplexer_1_out;

  Multiplexer #(.select(1), .width(4), .disabled("Z"), .enable("false")) multiplexer_1 (
    .in0(Din1), .in1(4'b0000), .out(multiplexer_1_out), .sel(\同步清零_气泡_高电平有效 ));
  Pull_Resistor #(.pull(0)) pull_resistor_1 (.node(\同步清零_气泡_高电平有效 ));
  not not_1 (not_1_out, \使能端_低电平有效_stall_高电平有效 );
  Register #(.width(4), .trigger("rising"), .Select("low")) register_1 (
    .D(multiplexer_1_out), .en(not_1_out), .Q(Dout1), .clk(CLK));  // open: clr
  Pull_Resistor #(.pull(0)) pull_resistor_2 (.node(not_1_out));
endmodule
module ID_EX (
  input  RegWrite,
  input  [3:0] AluOP,
  input  MemToReg,
  input  AluSrcB,
  input  [31:0] PC,
  input  [31:0] A,
  input  [31:0] B,
  input  [31:0] Imm,
  input  [4:0] Shamt,
  input  [4:0] W_num,
  input  MemWrite,
  input  JR,
  input  JMP,
  input  JAL,
  input  Beq,
  input  Bne,
  input  Syscall,
  input  [31:0] JAddr,
  input  [5:0] Op,
  input  [4:0] DataRedirect,
  input  [31:0] ID_PC,
  input  CLK,
  input  \同步清零_高电平有效 ,
  input  \使能端_低电平有效 ,
  output RegWriteOut,
  output [3:0] AluOPOut,
  output MemToRegOut,
  output AluSrcBOut,
  output [31:0] PCOut,
  output [31:0] AOut,
  output [31:0] BOut,
  output [31:0] ImmOut,
  output [4:0] ShamtOut,
  output [4:0] W_Out,
  output MemWriteOut,
  output JROut,
  output JMPOut,
  output JALOut,
  output BeqOut,
  output BneOut,
  output EX_SysCall,
  output [31:0] JAddr_2,
  output [5:0] OpOut,
  output [4:0] DataDirectOut,
  output [31:0] EX_PC
);

  wire multiplexer_1_out, multiplexer_3_out, multiplexer_4_out, multiplexer_11_out, multiplexer_12_out,
       multiplexer_13_out, multiplexer_14_out, multiplexer_15_out, multiplexer_16_out, multiplexer_17_out,
       pull_resistor_2_node;
  wire [3:0] multiplexer_2_out;
  wire [4:0] multiplexer_9_out, multiplexer_10_out, multiplexer_20_out;
  wire [5:0] multiplexer_19_out;
  wire [31:0] multiplexer_5_out, multiplexer_6_out, multiplexer_7_out, multiplexer_8_out, multiplexer_18_out,
       multiplexer_21_out;

  Multiplexer #(.select(1), .width(1), .disabled("Z"), .enable("false")) multiplexer_1 (
    .in0(RegWrite), .in1(1'b0), .out(multiplexer_1_out), .sel(\同步清零_高电平有效 ));
  Multiplexer #(.select(1), .width(4), .disabled("Z"), .enable("false")) multiplexer_2 (
    .in0(AluOP), .in1(4'b0000), .out(multiplexer_2_out), .sel(\同步清零_高电平有效 ));
  Multiplexer #(.select(1), .width(1), .disabled("Z"), .enable("false")) multiplexer_3 (
    .in0(MemToReg), .in1(1'b0), .out(multiplexer_3_out), .sel(\同步清零_高电平有效 ));
  Multiplexer #(.select(1), .width(1), .disabled("Z"), .enable("false")) multiplexer_4 (
    .in0(AluSrcB), .in1(1'b0), .out(multiplexer_4_out), .sel(\同步清零_高电平有效 ));
  Multiplexer #(.select(1), .width(32), .disabled("Z"), .enable("false")) multiplexer_5 (
    .in0(PC), .in1({32{1'b0}}), .out(multiplexer_5_out), .sel(\同步清零_高电平有效 ));
  Multiplexer #(.select(1), .width(32), .disabled("Z"), .enable("false")) multiplexer_6 (
    .in0(A), .in1({32{1'b0}}), .out(multiplexer_6_out), .sel(\同步清零_高电平有效 ));
  Multiplexer #(.select(1), .width(32), .disabled("Z"), .enable("false")) multiplexer_7 (
    .in0(B), .in1({32{1'b0}}), .out(multiplexer_7_out), .sel(\同步清零_高电平有效 ));
  Multiplexer #(.select(1), .width(32), .disabled("Z"), .enable("false")) multiplexer_8 (
    .in0(Imm), .in1({32{1'b0}}), .out(multiplexer_8_out), .sel(\同步清零_高电平有效 ));
  Multiplexer #(.select(1), .width(5), .disabled("Z"), .enable("false")) multiplexer_9 (
    .in0(Shamt), .in1({5{1'b0}}), .out(multiplexer_9_out), .sel(\同步清零_高电平有效 ));
  Multiplexer #(.select(1), .width(5), .disabled("Z"), .enable("false")) multiplexer_10 (
    .in0(W_num), .in1({5{1'b0}}), .out(multiplexer_10_out), .sel(\同步清零_高电平有效 ));
  Multiplexer #(.select(1), .width(1), .disabled("Z"), .enable("false")) multiplexer_11 (
    .in0(MemWrite), .in1(1'b0), .out(multiplexer_11_out), .sel(\同步清零_高电平有效 ));
  Multiplexer #(.select(1), .width(1), .disabled("Z"), .enable("false")) multiplexer_12 (
    .in0(JR), .in1(1'b0), .out(multiplexer_12_out), .sel(\同步清零_高电平有效 ));
  Multiplexer #(.select(1), .width(1), .disabled("Z"), .enable("false")) multiplexer_13 (
    .in0(JMP), .in1(1'b0), .out(multiplexer_13_out), .sel(\同步清零_高电平有效 ));
  Multiplexer #(.select(1), .width(1), .disabled("Z"), .enable("false")) multiplexer_14 (
    .in0(JAL), .in1(1'b0), .out(multiplexer_14_out), .sel(\同步清零_高电平有效 ));
  Multiplexer #(.select(1), .width(1), .disabled("Z"), .enable("false")) multiplexer_15 (
    .in0(Beq), .in1(1'b0), .out(multiplexer_15_out), .sel(\同步清零_高电平有效 ));
  Multiplexer #(.select(1), .width(1), .disabled("Z"), .enable("false")) multiplexer_16 (
    .in0(Bne), .in1(1'b0), .out(multiplexer_16_out), .sel(\同步清零_高电平有效 ));
  Multiplexer #(.select(1), .width(1), .disabled("Z"), .enable("false")) multiplexer_17 (
    .in0(Syscall), .in1(1'b0), .out(multiplexer_17_out), .sel(\同步清零_高电平有效 ));
  Multiplexer #(.select(1), .width(32), .disabled("Z"), .enable("false")) multiplexer_18 (
    .in0(JAddr), .in1({32{1'b0}}), .out(multiplexer_18_out), .sel(\同步清零_高电平有效 ));
  Multiplexer #(.select(1), .width(6), .disabled("Z"), .enable("false")) multiplexer_19 (
    .in0(Op), .in1({6{1'b0}}), .out(multiplexer_19_out), .sel(\同步清零_高电平有效 ));
  Multiplexer #(.select(1), .width(5), .disabled("Z"), .enable("false")) multiplexer_20 (
    .in0(DataRedirect), .in1({5{1'b0}}), .out(multiplexer_20_out), .sel(\同步清零_高电平有效 ));
  Multiplexer #(.select(1), .width(32), .disabled("Z"), .enable("false")) multiplexer_21 (
    .in0(ID_PC), .in1({32{1'b0}}), .out(multiplexer_21_out), .sel(\同步清零_高电平有效 ));
  Pull_Resistor #(.pull(0)) pull_resistor_1 (.node(\同步清零_高电平有效 ));
  Register #(.width(1), .trigger("rising"), .Select("low")) register_1 (
    .D(multiplexer_1_out), .en(pull_resistor_2_node), .Q(RegWriteOut), .clk(CLK));  // open: clr
  Register #(.width(4), .trigger("rising"), .Select("low")) register_2 (
    .D(multiplexer_2_out), .en(pull_resistor_2_node), .Q(AluOPOut), .clk(CLK));  // open: clr
  Register #(.width(1), .trigger("rising"), .Select("low")) register_3 (
    .D(multiplexer_3_out), .en(pull_resistor_2_node), .Q(MemToRegOut), .clk(CLK));  // open: clr
  Register #(.width(1), .trigger("rising"), .Select("low")) register_4 (
    .D(multiplexer_4_out), .en(pull_resistor_2_node), .Q(AluSrcBOut), .clk(CLK));  // open: clr
  Register #(.width(32), .trigger("rising"), .Select("low")) register_5 (
    .D(multiplexer_5_out), .en(pull_resistor_2_node), .Q(PCOut), .clk(CLK));  // open: clr
  Register #(.width(32), .trigger("rising"), .Select("low")) register_6 (
    .D(multiplexer_6_out), .en(pull_resistor_2_node), .Q(AOut), .clk(CLK));  // open: clr
  Register #(.width(32), .trigger("rising"), .Select("low")) register_7 (
    .D(multiplexer_7_out), .en(pull_resistor_2_node), .Q(BOut), .clk(CLK));  // open: clr
  Register #(.width(32), .trigger("rising"), .Select("low")) register_8 (
    .D(multiplexer_8_out), .en(pull_resistor_2_node), .Q(ImmOut), .clk(CLK));  // open: clr
  Register #(.width(5), .trigger("rising"), .Select("low")) register_9 (
    .D(multiplexer_9_out), .en(pull_resistor_2_node), .Q(ShamtOut), .clk(CLK));  // open: clr
  Register #(.width(5), .trigger("rising"), .Select("low")) register_10 (
    .D(multiplexer_10_out), .en(pull_resistor_2_node), .Q(W_Out), .clk(CLK));  // open: clr
  Register #(.width(1), .trigger("rising"), .Select("low")) register_11 (
    .D(multiplexer_11_out), .en(pull_resistor_2_node), .Q(MemWriteOut), .clk(CLK));  // open: clr
  Register #(.width(1), .trigger("rising"), .Select("low")) register_12 (
    .D(multiplexer_12_out), .en(pull_resistor_2_node), .Q(JROut), .clk(CLK));  // open: clr
  Register #(.width(1), .trigger("rising"), .Select("low")) register_13 (
    .D(multiplexer_13_out), .en(pull_resistor_2_node), .Q(JMPOut), .clk(CLK));  // open: clr
  Register #(.width(1), .trigger("rising"), .Select("low")) register_14 (
    .D(multiplexer_14_out), .en(pull_resistor_2_node), .Q(JALOut), .clk(CLK));  // open: clr
  Register #(.width(1), .trigger("rising"), .Select("low")) register_15 (
    .D(multiplexer_15_out), .en(pull_resistor_2_node), .Q(BeqOut), .clk(CLK));  // open: clr
  Register #(.width(1), .trigger("rising"), .Select("low")) register_16 (
    .D(multiplexer_16_out), .en(pull_resistor_2_node), .Q(BneOut), .clk(CLK));  // open: clr
  Register #(.width(1), .trigger("rising"), .Select("low")) register_17 (
    .D(multiplexer_17_out), .en(pull_resistor_2_node), .Q(EX_SysCall), .clk(CLK));  // open: clr
  Register #(.width(32), .trigger("rising"), .Select("low")) register_18 (
    .D(multiplexer_18_out), .en(pull_resistor_2_node), .Q(JAddr_2), .clk(CLK));  // open: clr
  Register #(.width(6), .trigger("rising"), .Select("low")) register_19 (
    .D(multiplexer_19_out), .en(pull_resistor_2_node), .Q(OpOut), .clk(CLK));  // open: clr
  Register #(.width(5), .trigger("rising"), .Select("low")) register_20 (
    .D(multiplexer_20_out), .en(pull_resistor_2_node), .Q(DataDirectOut), .clk(CLK));  // open: clr
  Register #(.width(32), .trigger("rising"), .Select("low")) register_21 (
    .D(multiplexer_21_out), .en(pull_resistor_2_node), .Q(EX_PC), .clk(CLK));  // open: clr
  Pull_Resistor #(.pull(0)) pull_resistor_2 (.node(pull_resistor_2_node));
  not not_1 (pull_resistor_2_node, \使能端_低电平有效 );

  // Notes on the sheet:
  //   同步清零_高电平有效: pull=down
  //   使能端_低电平有效: pull=down
  //   下拉电阻使得引脚可以悬空
endmodule

module IF_ID (
  input  [31:0] PC_4,
  input  [31:0] RD,
  input  [31:0] JAddr,
  input  CLK,
  input  \同步清零_高电平有效 ,
  input  \使能端_低电平有效 ,
  output [31:0] PC_4Out,
  output [31:0] RDOut,
  output [31:0] JAddrOut
);

  wire pull_resistor_2_node;
  wire [31:0] multiplexer_1_out, multiplexer_2_out, multiplexer_3_out;

  Multiplexer #(.select(1), .width(32), .disabled("Z"), .enable("false")) multiplexer_1 (
    .in0(PC_4), .in1({32{1'b0}}), .out(multiplexer_1_out), .sel(\同步清零_高电平有效 ));
  Multiplexer #(.select(1), .width(32), .disabled("Z"), .enable("false")) multiplexer_2 (
    .in0(RD), .in1({32{1'b0}}), .out(multiplexer_2_out), .sel(\同步清零_高电平有效 ));
  Multiplexer #(.select(1), .width(32), .disabled("Z"), .enable("false")) multiplexer_3 (
    .in0(JAddr), .in1({32{1'b0}}), .out(multiplexer_3_out), .sel(\同步清零_高电平有效 ));
  Pull_Resistor #(.pull(0)) pull_resistor_1 (.node(\同步清零_高电平有效 ));
  Register #(.width(32), .trigger("rising"), .Select("low")) register_1 (
    .D(multiplexer_1_out), .en(pull_resistor_2_node), .Q(PC_4Out), .clk(CLK));  // open: clr
  Register #(.width(32), .trigger("rising"), .Select("low")) register_2 (
    .D(multiplexer_2_out), .en(pull_resistor_2_node), .Q(RDOut), .clk(CLK));  // open: clr
  Register #(.width(32), .trigger("rising"), .Select("low")) register_3 (
    .D(multiplexer_3_out), .en(pull_resistor_2_node), .Q(JAddrOut), .clk(CLK));  // open: clr
  Pull_Resistor #(.pull(0)) pull_resistor_2 (.node(pull_resistor_2_node));
  not not_1 (pull_resistor_2_node, \使能端_低电平有效 );

  // Notes on the sheet:
  //   同步清零_高电平有效: pull=down
  //   使能端_低电平有效: pull=down
  //   下拉电阻使得引脚可以悬空
endmodule

module EX_MEM (
  input  RegWrite,
  input  [31:0] PC_4,
  input  MenToReg,
  input  [31:0] AluOut,
  input  [31:0] B,
  input  [4:0] W_num,
  input  MemWrite,
  input  JAL,
  input  EX_Halt,
  input  [5:0] Op,
  input  [31:0] EX_PC,
  input  CLK,
  input  \同步清零_高电平有效 ,
  input  \使能端_低电平有效 ,
  output RegWriteOut,
  output [31:0] PCOut,
  output MenToRegOut,
  output [31:0] AluOut_2,
  output [31:0] BOut,
  output [4:0] W_Out,
  output MemWriteOut,
  output JALOut,
  output MEM_Halt,
  output [5:0] OpOut,
  output [31:0] MEM_PC
);

  wire multiplexer_1_out, multiplexer_3_out, multiplexer_7_out, multiplexer_8_out, multiplexer_9_out,
       pull_resistor_2_node;
  wire [4:0] multiplexer_6_out;
  wire [5:0] multiplexer_10_out;
  wire [31:0] multiplexer_2_out, multiplexer_4_out, multiplexer_5_out, multiplexer_11_out;

  Multiplexer #(.select(1), .width(1), .disabled("Z"), .enable("false")) multiplexer_1 (
    .in0(RegWrite), .in1(1'b0), .out(multiplexer_1_out), .sel(\同步清零_高电平有效 ));
  Multiplexer #(.select(1), .width(32), .disabled("Z"), .enable("false")) multiplexer_2 (
    .in0(PC_4), .in1({32{1'b0}}), .out(multiplexer_2_out), .sel(\同步清零_高电平有效 ));
  Multiplexer #(.select(1), .width(1), .disabled("Z"), .enable("false")) multiplexer_3 (
    .in0(MenToReg), .in1(1'b0), .out(multiplexer_3_out), .sel(\同步清零_高电平有效 ));
  Multiplexer #(.select(1), .width(32), .disabled("Z"), .enable("false")) multiplexer_4 (
    .in0(AluOut), .in1({32{1'b0}}), .out(multiplexer_4_out), .sel(\同步清零_高电平有效 ));
  Multiplexer #(.select(1), .width(32), .disabled("Z"), .enable("false")) multiplexer_5 (
    .in0(B), .in1({32{1'b0}}), .out(multiplexer_5_out), .sel(\同步清零_高电平有效 ));
  Multiplexer #(.select(1), .width(5), .disabled("Z"), .enable("false")) multiplexer_6 (
    .in0(W_num), .in1({5{1'b0}}), .out(multiplexer_6_out), .sel(\同步清零_高电平有效 ));
  Multiplexer #(.select(1), .width(1), .disabled("Z"), .enable("false")) multiplexer_7 (
    .in0(MemWrite), .in1(1'b0), .out(multiplexer_7_out), .sel(\同步清零_高电平有效 ));
  Multiplexer #(.select(1), .width(1), .disabled("Z"), .enable("false")) multiplexer_8 (
    .in0(JAL), .in1(1'b0), .out(multiplexer_8_out), .sel(\同步清零_高电平有效 ));
  Multiplexer #(.select(1), .width(1), .disabled("Z"), .enable("false")) multiplexer_9 (
    .in0(EX_Halt), .in1(1'b0), .out(multiplexer_9_out), .sel(\同步清零_高电平有效 ));
  Multiplexer #(.select(1), .width(6), .disabled("Z"), .enable("false")) multiplexer_10 (
    .in0(Op), .in1({6{1'b0}}), .out(multiplexer_10_out), .sel(\同步清零_高电平有效 ));
  Multiplexer #(.select(1), .width(32), .disabled("Z"), .enable("false")) multiplexer_11 (
    .in0(EX_PC), .in1({32{1'b0}}), .out(multiplexer_11_out), .sel(\同步清零_高电平有效 ));
  Pull_Resistor #(.pull(0)) pull_resistor_1 (.node(\同步清零_高电平有效 ));
  Register #(.width(1), .trigger("rising"), .Select("low")) register_1 (
    .D(multiplexer_1_out), .en(pull_resistor_2_node), .Q(RegWriteOut), .clk(CLK));  // open: clr
  Register #(.width(32), .trigger("rising"), .Select("low")) register_2 (
    .D(multiplexer_2_out), .en(pull_resistor_2_node), .Q(PCOut), .clk(CLK));  // open: clr
  Register #(.width(1), .trigger("rising"), .Select("low")) register_3 (
    .D(multiplexer_3_out), .en(pull_resistor_2_node), .Q(MenToRegOut), .clk(CLK));  // open: clr
  Register #(.width(32), .trigger("rising"), .Select("low")) register_4 (
    .D(multiplexer_4_out), .en(pull_resistor_2_node), .Q(AluOut_2), .clk(CLK));  // open: clr
  Register #(.width(32), .trigger("rising"), .Select("low")) register_5 (
    .D(multiplexer_5_out), .en(pull_resistor_2_node), .Q(BOut), .clk(CLK));  // open: clr
  Register #(.width(5), .trigger("rising"), .Select("low")) register_6 (
    .D(multiplexer_6_out), .en(pull_resistor_2_node), .Q(W_Out), .clk(CLK));  // open: clr
  Register #(.width(1), .trigger("rising"), .Select("low")) register_7 (
    .D(multiplexer_7_out), .en(pull_resistor_2_node), .Q(MemWriteOut), .clk(CLK));  // open: clr
  Register #(.width(1), .trigger("rising"), .Select("low")) register_8 (
    .D(multiplexer_8_out), .en(pull_resistor_2_node), .Q(JALOut), .clk(CLK));  // open: clr
  Register #(.width(1), .trigger("rising"), .Select("low")) register_9 (
    .D(multiplexer_9_out), .en(pull_resistor_2_node), .Q(MEM_Halt), .clk(CLK));  // open: clr
  Register #(.width(6), .trigger("rising"), .Select("low")) register_10 (
    .D(multiplexer_10_out), .en(pull_resistor_2_node), .Q(OpOut), .clk(CLK));  // open: clr
  Register #(.width(32), .trigger("rising"), .Select("low")) register_11 (
    .D(multiplexer_11_out), .en(pull_resistor_2_node), .Q(MEM_PC), .clk(CLK));  // open: clr
  Pull_Resistor #(.pull(0)) pull_resistor_2 (.node(pull_resistor_2_node));
  not not_1 (pull_resistor_2_node, \使能端_低电平有效 );

  // Notes on the sheet:
  //   同步清零_高电平有效: pull=down
  //   使能端_低电平有效: pull=down
  //   下拉电阻使得引脚可以悬空
endmodule

module MEM_WB (
  input  RegWrite,
  input  MenToReg,
  input  MEM_Halt,
  input  [31:0] MemOut,
  input  [31:0] AluOut,
  input  [4:0] W_num,
  input  JAL,
  input  [31:0] PC_4,
  input  [5:0] Op,
  input  [31:0] MEM_PC,
  input  CLK,
  input  \同步清零_高电平有效 ,
  input  \使能端_低电平有效 ,
  output RegWriteOut,
  output MenToRegOut,
  output WB_Halt,
  output [31:0] MenOut,
  output [31:0] AluOut_2,
  output [4:0] W_Out,
  output JALOut,
  output [31:0] PCOut,
  output [5:0] OpOut,
  output [31:0] WB_PC
);

  wire multiplexer_1_out, multiplexer_2_out, multiplexer_3_out, multiplexer_7_out, pull_resistor_2_node;
  wire [4:0] multiplexer_6_out;
  wire [5:0] multiplexer_9_out;
  wire [31:0] multiplexer_4_out, multiplexer_5_out, multiplexer_8_out, multiplexer_10_out;

  Multiplexer #(.select(1), .width(1), .disabled("Z"), .enable("false")) multiplexer_1 (
    .in0(RegWrite), .in1(1'b0), .out(multiplexer_1_out), .sel(\同步清零_高电平有效 ));
  Multiplexer #(.select(1), .width(1), .disabled("Z"), .enable("false")) multiplexer_2 (
    .in0(MenToReg), .in1(1'b0), .out(multiplexer_2_out), .sel(\同步清零_高电平有效 ));
  Multiplexer #(.select(1), .width(1), .disabled("Z"), .enable("false")) multiplexer_3 (
    .in0(MEM_Halt), .in1(1'b0), .out(multiplexer_3_out), .sel(\同步清零_高电平有效 ));
  Multiplexer #(.select(1), .width(32), .disabled("Z"), .enable("false")) multiplexer_4 (
    .in0(MemOut), .in1({32{1'b0}}), .out(multiplexer_4_out), .sel(\同步清零_高电平有效 ));
  Multiplexer #(.select(1), .width(32), .disabled("Z"), .enable("false")) multiplexer_5 (
    .in0(AluOut), .in1({32{1'b0}}), .out(multiplexer_5_out), .sel(\同步清零_高电平有效 ));
  Multiplexer #(.select(1), .width(5), .disabled("Z"), .enable("false")) multiplexer_6 (
    .in0(W_num), .in1({5{1'b0}}), .out(multiplexer_6_out), .sel(\同步清零_高电平有效 ));
  Multiplexer #(.select(1), .width(1), .disabled("Z"), .enable("false")) multiplexer_7 (
    .in0(JAL), .in1(1'b0), .out(multiplexer_7_out), .sel(\同步清零_高电平有效 ));
  Multiplexer #(.select(1), .width(32), .disabled("Z"), .enable("false")) multiplexer_8 (
    .in0(PC_4), .in1({32{1'b0}}), .out(multiplexer_8_out), .sel(\同步清零_高电平有效 ));
  Multiplexer #(.select(1), .width(6), .disabled("Z"), .enable("false")) multiplexer_9 (
    .in0(Op), .in1({6{1'b0}}), .out(multiplexer_9_out), .sel(\同步清零_高电平有效 ));
  Multiplexer #(.select(1), .width(32), .disabled("Z"), .enable("false")) multiplexer_10 (
    .in0(MEM_PC), .in1({32{1'b0}}), .out(multiplexer_10_out), .sel(\同步清零_高电平有效 ));
  Pull_Resistor #(.pull(0)) pull_resistor_1 (.node(\同步清零_高电平有效 ));
  Register #(.width(1), .trigger("rising"), .Select("low")) register_1 (
    .D(multiplexer_1_out), .en(pull_resistor_2_node), .Q(RegWriteOut), .clk(CLK));  // open: clr
  Register #(.width(1), .trigger("rising"), .Select("low")) register_2 (
    .D(multiplexer_2_out), .en(pull_resistor_2_node), .Q(MenToRegOut), .clk(CLK));  // open: clr
  Register #(.width(1), .trigger("rising"), .Select("low")) register_3 (
    .D(multiplexer_3_out), .en(pull_resistor_2_node), .Q(WB_Halt), .clk(CLK));  // open: clr
  Register #(.width(32), .trigger("rising"), .Select("low")) register_4 (
    .D(multiplexer_4_out), .en(pull_resistor_2_node), .Q(MenOut), .clk(CLK));  // open: clr
  Register #(.width(32), .trigger("rising"), .Select("low")) register_5 (
    .D(multiplexer_5_out), .en(pull_resistor_2_node), .Q(AluOut_2), .clk(CLK));  // open: clr
  Register #(.width(5), .trigger("rising"), .Select("low")) register_6 (
    .D(multiplexer_6_out), .en(pull_resistor_2_node), .Q(W_Out), .clk(CLK));  // open: clr
  Register #(.width(1), .trigger("rising"), .Select("low")) register_7 (
    .D(multiplexer_7_out), .en(pull_resistor_2_node), .Q(JALOut), .clk(CLK));  // open: clr
  Register #(.width(32), .trigger("rising"), .Select("low")) register_8 (
    .D(multiplexer_8_out), .en(pull_resistor_2_node), .Q(PCOut), .clk(CLK));  // open: clr
  Register #(.width(6), .trigger("rising"), .Select("low")) register_9 (
    .D(multiplexer_9_out), .en(pull_resistor_2_node), .Q(OpOut), .clk(CLK));  // open: clr
  Register #(.width(32), .trigger("rising"), .Select("low")) register_10 (
    .D(multiplexer_10_out), .en(pull_resistor_2_node), .Q(WB_PC), .clk(CLK));  // open: clr
  Pull_Resistor #(.pull(0)) pull_resistor_2 (.node(pull_resistor_2_node));
  not not_1 (pull_resistor_2_node, \使能端_低电平有效 );

  // Notes on the sheet:
  //   使能端_低电平有效: pull=down
  //   同步清零_高电平有效: pull=down
  //   下拉电阻使得引脚可以悬空
endmodule

module \源寄存器使用情况  (
  input  OP0,
  input  OP1,
  input  OP2,
  input  OP3,
  input  OP4,
  input  OP5,
  input  F0,
  input  F1,
  input  F2,
  input  F3,
  input  F4,
  input  F5,
  output R1_Used,
  output R2_Used
);

  wire and_1_out, and_2_out, and_3_out, and_4_out, and_5_out, and_6_out, and_7_out, and_8_out, and_9_out,
       and_10_out, and_11_out, and_12_out, and_13_out, and_14_out, and_15_out, and_16_out, and_17_out,
       and_18_out, and_19_out, and_20_out, and_21_out, and_22_out, and_23_out, and_24_out, and_25_out,
       and_26_out, and_27_out, and_28_out, and_29_out, and_30_out, and_31_out, and_32_out, and_33_out,
       and_34_out, not_1_out, not_2_out, not_3_out, not_4_out, not_5_out, not_6_out, not_7_out, not_8_out,
       not_9_out, not_10_out, not_11_out, not_12_out, not_13_out, not_14_out, not_15_out, not_16_out,
       not_17_out, not_18_out, not_19_out, not_20_out, not_21_out, not_22_out, not_23_out, not_24_out,
       not_25_out, not_26_out, not_27_out, not_28_out, not_29_out, not_30_out, not_31_out, not_32_out,
       not_33_out, not_34_out, not_35_out, not_36_out, not_37_out, not_38_out, not_39_out, not_40_out,
       not_41_out, not_42_out, not_43_out, not_44_out, not_45_out, not_46_out, not_47_out, not_48_out,
       not_49_out, not_50_out, not_51_out, not_52_out, not_53_out, not_54_out, not_55_out, not_56_out,
       not_57_out, not_58_out, not_59_out, not_60_out, not_61_out, not_62_out, not_63_out, not_64_out,
       not_65_out, not_66_out, not_67_out, not_68_out, not_69_out, not_70_out, not_71_out, not_72_out,
       not_73_out, not_74_out, not_75_out, not_76_out, not_77_out, not_78_out, not_79_out, not_80_out,
       not_81_out, not_82_out, not_83_out, not_84_out, not_85_out, not_86_out, not_87_out, not_88_out,
       not_89_out, not_90_out, not_91_out, not_92_out, not_93_out, not_94_out, not_95_out, not_96_out,
       not_97_out, not_98_out, not_99_out, not_100_out, not_101_out, not_102_out, not_103_out, not_104_out,
       not_105_out, not_106_out, not_107_out, not_108_out, not_109_out, not_110_out, not_111_out,
       not_112_out, not_113_out, not_114_out, not_115_out, not_116_out, not_117_out, not_118_out,
       not_119_out, not_120_out, not_121_out, not_122_out, not_123_out, not_124_out, not_125_out,
       not_126_out, not_127_out, not_128_out, not_129_out, not_130_out, not_131_out, not_132_out,
       not_133_out, not_134_out, not_135_out, not_136_out, not_137_out, not_138_out, not_139_out,
       not_140_out, not_141_out, not_142_out, not_143_out, not_144_out, not_145_out, not_146_out,
       not_147_out, not_148_out, not_149_out, not_150_out, not_151_out, not_152_out, not_153_out,
       not_154_out, not_155_out, not_156_out, not_157_out, not_158_out, not_159_out, not_160_out,
       not_161_out, not_162_out, not_163_out, not_164_out, not_165_out, not_166_out, not_167_out,
       not_168_out, not_169_out, not_170_out, not_171_out, not_172_out, not_173_out, not_174_out,
       not_175_out, not_176_out, not_177_out, not_178_out, not_179_out, not_180_out, not_181_out,
       not_182_out, not_183_out, not_184_out, not_185_out, not_186_out, not_187_out, not_188_out,
       not_189_out, not_190_out, not_191_out, not_192_out, not_193_out, not_194_out, not_195_out,
       not_196_out, not_197_out, not_198_out, not_199_out, not_200_out, not_201_out, not_202_out,
       not_203_out, not_204_out, not_205_out, not_206_out, not_207_out, not_208_out, not_209_out,
       not_210_out, not_211_out, not_212_out, not_213_out, not_214_out, not_215_out, not_216_out,
       not_217_out, not_218_out, not_219_out, not_220_out, not_221_out, not_222_out, not_223_out,
       not_224_out, not_225_out, not_226_out, not_227_out, not_228_out, not_229_out, not_230_out,
       not_231_out, not_232_out, not_233_out, not_234_out, not_235_out, not_236_out, not_237_out,
       not_238_out, not_239_out, not_240_out, not_241_out, not_242_out, not_243_out, not_244_out,
       not_245_out, not_246_out, not_247_out, not_248_out, not_249_out, not_250_out, not_251_out,
       not_252_out, not_253_out, not_254_out, not_255_out, not_256_out, not_257_out, not_258_out, not_259_out;

  not not_1 (not_1_out, OP5);
  not not_2 (not_2_out, OP4);
  not not_3 (not_3_out, OP3);
  not not_4 (not_4_out, OP2);
  not not_5 (not_5_out, OP1);
  not not_6 (not_6_out, OP0);
  not not_7 (not_7_out, F4);
  not not_8 (not_8_out, F3);
  not not_9 (not_9_out, F2);
  not not_10 (not_10_out, F1);
  not not_11 (not_11_out, F0);
  not not_12 (not_12_out, OP5);
  not not_13 (not_13_out, OP4);
  not not_14 (not_14_out, OP3);
  not not_15 (not_15_out, OP2);
  not not_16 (not_16_out, OP1);
  not not_17 (not_17_out, OP0);
  not not_18 (not_18_out, F4);
  not not_19 (not_19_out, F3);
  not not_20 (not_20_out, F2);
  not not_21 (not_21_out, F1);
  not not_22 (not_22_out, OP5);
  not not_23 (not_23_out, OP4);
  not not_24 (not_24_out, OP3);
  not not_25 (not_25_out, OP2);
  not not_26 (not_26_out, OP1);
  not not_27 (not_27_out, OP0);
  not not_28 (not_28_out, F4);
  not not_29 (not_29_out, F3);
  not not_30 (not_30_out, F2);
  not not_31 (not_31_out, F0);
  not not_32 (not_32_out, OP5);
  not not_33 (not_33_out, OP4);
  not not_34 (not_34_out, OP3);
  not not_35 (not_35_out, OP2);
  not not_36 (not_36_out, OP1);
  not not_37 (not_37_out, OP0);
  not not_38 (not_38_out, F4);
  not not_39 (not_39_out, F3);
  not not_40 (not_40_out, F1);
  not not_41 (not_41_out, F0);
  not not_42 (not_42_out, OP5);
  not not_43 (not_43_out, OP4);
  not not_44 (not_44_out, OP3);
  not not_45 (not_45_out, OP2);
  not not_46 (not_46_out, OP1);
  not not_47 (not_47_out, OP0);
  not not_48 (not_48_out, F4);
  not not_49 (not_49_out, F3);
  not not_50 (not_50_out, F1);
  not not_51 (not_51_out, OP5);
  not not_52 (not_52_out, OP4);
  not not_53 (not_53_out, OP3);
  not not_54 (not_54_out, OP2);
  not not_55 (not_55_out, OP1);
  not not_56 (not_56_out, OP0);
  not not_57 (not_57_out, F4);
  not not_58 (not_58_out, F3);
  not not_59 (not_59_out, OP5);
  not not_60 (not_60_out, OP4);
  not not_61 (not_61_out, OP3);
  not not_62 (not_62_out, OP2);
  not not_63 (not_63_out, OP1);
  not not_64 (not_64_out, OP0);
  not not_65 (not_65_out, F4);
  not not_66 (not_66_out, F2);
  not not_67 (not_67_out, F0);
  not not_68 (not_68_out, OP5);
  not not_69 (not_69_out, OP4);
  not not_70 (not_70_out, OP3);
  not not_71 (not_71_out, OP2);
  not not_72 (not_72_out, OP1);
  not not_73 (not_73_out, OP0);
  not not_74 (not_74_out, F4);
  not not_75 (not_75_out, F2);
  not not_76 (not_76_out, OP5);
  not not_77 (not_77_out, OP4);
  not not_78 (not_78_out, OP3);
  not not_79 (not_79_out, OP2);
  not not_80 (not_80_out, OP1);
  not not_81 (not_81_out, OP0);
  not not_82 (not_82_out, F5);
  not not_83 (not_83_out, F4);
  not not_84 (not_84_out, F2);
  not not_85 (not_85_out, F1);
  not not_86 (not_86_out, F0);
  not not_87 (not_87_out, OP5);
  not not_88 (not_88_out, OP4);
  not not_89 (not_89_out, OP3);
  not not_90 (not_90_out, OP2);
  not not_91 (not_91_out, OP1);
  not not_92 (not_92_out, OP0);
  not not_93 (not_93_out, F5);
  not not_94 (not_94_out, F4);
  not not_95 (not_95_out, F1);
  not not_96 (not_96_out, F0);
  not not_97 (not_97_out, OP5);
  not not_98 (not_98_out, OP4);
  not not_99 (not_99_out, OP3);
  not not_100 (not_100_out, OP1);
  not not_101 (not_101_out, OP0);
  not not_102 (not_102_out, OP5);
  not not_103 (not_103_out, OP4);
  not not_104 (not_104_out, OP3);
  not not_105 (not_105_out, OP1);
  not not_106 (not_106_out, OP5);
  not not_107 (not_107_out, OP4);
  not not_108 (not_108_out, OP2);
  not not_109 (not_109_out, OP1);
  not not_110 (not_110_out, OP0);
  not not_111 (not_111_out, OP5);
  not not_112 (not_112_out, OP4);
  not not_113 (not_113_out, OP1);
  not not_114 (not_114_out, OP0);
  not not_115 (not_115_out, OP5);
  not not_116 (not_116_out, OP4);
  not not_117 (not_117_out, OP2);
  not not_118 (not_118_out, OP1);
  not not_119 (not_119_out, OP5);
  not not_120 (not_120_out, OP4);
  not not_121 (not_121_out, OP2);
  not not_122 (not_122_out, OP0);
  not not_123 (not_123_out, OP5);
  not not_124 (not_124_out, OP4);
  not not_125 (not_125_out, OP1);
  not not_126 (not_126_out, OP4);
  not not_127 (not_127_out, OP3);
  not not_128 (not_128_out, OP2);
  not not_129 (not_129_out, OP4);
  not not_130 (not_130_out, OP2);
  not not_131 (not_131_out, OP5);
  not not_132 (not_132_out, OP4);
  not not_133 (not_133_out, OP3);
  not not_134 (not_134_out, OP2);
  not not_135 (not_135_out, OP1);
  not not_136 (not_136_out, OP0);
  not not_137 (not_137_out, F5);
  not not_138 (not_138_out, F4);
  not not_139 (not_139_out, F3);
  not not_140 (not_140_out, F2);
  not not_141 (not_141_out, F1);
  not not_142 (not_142_out, F0);
  not not_143 (not_143_out, OP5);
  not not_144 (not_144_out, OP4);
  not not_145 (not_145_out, OP3);
  not not_146 (not_146_out, OP2);
  not not_147 (not_147_out, OP1);
  not not_148 (not_148_out, OP0);
  not not_149 (not_149_out, F5);
  not not_150 (not_150_out, F4);
  not not_151 (not_151_out, F3);
  not not_152 (not_152_out, F2);
  not not_153 (not_153_out, OP5);
  not not_154 (not_154_out, OP4);
  not not_155 (not_155_out, OP3);
  not not_156 (not_156_out, OP2);
  not not_157 (not_157_out, OP1);
  not not_158 (not_158_out, OP0);
  not not_159 (not_159_out, F5);
  not not_160 (not_160_out, F4);
  not not_161 (not_161_out, F3);
  not not_162 (not_162_out, F2);
  not not_163 (not_163_out, F0);
  not not_164 (not_164_out, OP5);
  not not_165 (not_165_out, OP4);
  not not_166 (not_166_out, OP3);
  not not_167 (not_167_out, OP2);
  not not_168 (not_168_out, OP1);
  not not_169 (not_169_out, OP0);
  not not_170 (not_170_out, F4);
  not not_171 (not_171_out, F3);
  not not_172 (not_172_out, F2);
  not not_173 (not_173_out, F1);
  not not_174 (not_174_out, F0);
  not not_175 (not_175_out, OP5);
  not not_176 (not_176_out, OP4);
  not not_177 (not_177_out, OP3);
  not not_178 (not_178_out, OP2);
  not not_179 (not_179_out, OP1);
  not not_180 (not_180_out, OP0);
  not not_181 (not_181_out, F4);
  not not_182 (not_182_out, F3);
  not not_183 (not_183_out, F2);
  not not_184 (not_184_out, F1);
  not not_185 (not_185_out, OP5);
  not not_186 (not_186_out, OP4);
  not not_187 (not_187_out, OP3);
  not not_188 (not_188_out, OP2);
  not not_189 (not_189_out, OP1);
  not not_190 (not_190_out, OP0);
  not not_191 (not_191_out, F4);
  not not_192 (not_192_out, F3);
  not not_193 (not_193_out, F2);
  not not_194 (not_194_out, F0);
  not not_195 (not_195_out, OP5);
  not not_196 (not_196_out, OP4);
  not not_197 (not_197_out, OP3);
  not not_198 (not_198_out, OP2);
  not not_199 (not_199_out, OP1);
  not not_200 (not_200_out, OP0);
  not not_201 (not_201_out, F4);
  not not_202 (not_202_out, F3);
  not not_203 (not_203_out, F1);
  not not_204 (not_204_out, F0);
  not not_205 (not_205_out, OP5);
  not not_206 (not_206_out, OP4);
  not not_207 (not_207_out, OP3);
  not not_208 (not_208_out, OP2);
  not not_209 (not_209_out, OP1);
  not not_210 (not_210_out, OP0);
  not not_211 (not_211_out, F4);
  not not_212 (not_212_out, F3);
  not not_213 (not_213_out, F1);
  not not_214 (not_214_out, OP5);
  not not_215 (not_215_out, OP4);
  not not_216 (not_216_out, OP3);
  not not_217 (not_217_out, OP2);
  not not_218 (not_218_out, OP1);
  not not_219 (not_219_out, OP0);
  not not_220 (not_220_out, F4);
  not not_221 (not_221_out, F3);
  not not_222 (not_222_out, OP5);
  not not_223 (not_223_out, OP4);
  not not_224 (not_224_out, OP3);
  not not_225 (not_225_out, OP2);
  not not_226 (not_226_out, OP1);
  not not_227 (not_227_out, OP0);
  not not_228 (not_228_out, F4);
  not not_229 (not_229_out, F2);
  not not_230 (not_230_out, F0);
  not not_231 (not_231_out, OP5);
  not not_232 (not_232_out, OP4);
  not not_233 (not_233_out, OP3);
  not not_234 (not_234_out, OP2);
  not not_235 (not_235_out, OP1);
  not not_236 (not_236_out, OP0);
  not not_237 (not_237_out, F4);
  not not_238 (not_238_out, F2);
  not not_239 (not_239_out, OP5);
  not not_240 (not_240_out, OP4);
  not not_241 (not_241_out, OP3);
  not not_242 (not_242_out, OP2);
  not not_243 (not_243_out, OP1);
  not not_244 (not_244_out, OP0);
  not not_245 (not_245_out, F5);
  not not_246 (not_246_out, F4);
  not not_247 (not_247_out, F1);
  not not_248 (not_248_out, F0);
  not not_249 (not_249_out, OP5);
  not not_250 (not_250_out, OP4);
  not not_251 (not_251_out, OP3);
  not not_252 (not_252_out, OP1);
  not not_253 (not_253_out, OP0);
  not not_254 (not_254_out, OP5);
  not not_255 (not_255_out, OP4);
  not not_256 (not_256_out, OP3);
  not not_257 (not_257_out, OP1);
  not not_258 (not_258_out, OP4);
  not not_259 (not_259_out, OP2);
  and and_1 (and_1_out, not_1_out, not_2_out, not_3_out, not_4_out, not_5_out, not_6_out, F5, not_7_out, not_8_out, not_9_out, not_10_out, not_11_out);
  and and_2 (and_2_out, not_12_out, not_13_out, not_14_out, not_15_out, not_16_out, not_17_out, F5, not_18_out, not_19_out, not_20_out, not_21_out, F0);
  and and_3 (and_3_out, not_22_out, not_23_out, not_24_out, not_25_out, not_26_out, not_27_out, F5, not_28_out, not_29_out, not_30_out, F1, not_31_out);
  and and_4 (and_4_out, not_32_out, not_33_out, not_34_out, not_35_out, not_36_out, not_37_out, F5, not_38_out, not_39_out, F2, not_40_out, not_41_out);
  and and_5 (and_5_out, not_42_out, not_43_out, not_44_out, not_45_out, not_46_out, not_47_out, F5, not_48_out, not_49_out, F2, not_50_out, F0);
  and and_6 (and_6_out, not_51_out, not_52_out, not_53_out, not_54_out, not_55_out, not_56_out, F5, not_57_out, not_58_out, F2, F1, F0);
  and and_7 (and_7_out, not_59_out, not_60_out, not_61_out, not_62_out, not_63_out, not_64_out, F5, not_65_out, F3, not_66_out, F1, not_67_out);
  and and_8 (and_8_out, not_68_out, not_69_out, not_70_out, not_71_out, not_72_out, not_73_out, F5, not_74_out, F3, not_75_out, F1, F0);
  and and_9 (and_9_out, not_76_out, not_77_out, not_78_out, not_79_out, not_80_out, not_81_out, not_82_out, not_83_out, F3, not_84_out, not_85_out, not_86_out);
  and and_10 (and_10_out, not_87_out, not_88_out, not_89_out, not_90_out, not_91_out, not_92_out, not_93_out, not_94_out, F3, F2, not_95_out, not_96_out);
  and and_11 (and_11_out, not_97_out, not_98_out, not_99_out, OP2, not_100_out, not_101_out);
  and and_12 (and_12_out, not_102_out, not_103_out, not_104_out, OP2, not_105_out, OP0);
  and and_13 (and_13_out, not_106_out, not_107_out, OP3, not_108_out, not_109_out, not_110_out);
  and and_14 (and_14_out, not_111_out, not_112_out, OP3, OP2, not_113_out, not_114_out);
  and and_15 (and_15_out, not_115_out, not_116_out, OP3, not_117_out, not_118_out, OP0);
  and and_16 (and_16_out, not_119_out, not_120_out, OP3, not_121_out, OP1, not_122_out);
  and and_17 (and_17_out, not_123_out, not_124_out, OP3, OP2, not_125_out, OP0);
  and and_18 (and_18_out, OP5, not_126_out, not_127_out, not_128_out, OP1, OP0);
  and and_19 (and_19_out, OP5, not_129_out, OP3, not_130_out, OP1, OP0);
  and and_20 (and_20_out, not_131_out, not_132_out, not_133_out, not_134_out, not_135_out, not_136_out, not_137_out, not_138_out, not_139_out, not_140_out, not_141_out, not_142_out);
  and and_21 (and_21_out, not_143_out, not_144_out, not_145_out, not_146_out, not_147_out, not_148_out, not_149_out, not_150_out, not_151_out, not_152_out, F1, F0);
  and and_22 (and_22_out, not_153_out, not_154_out, not_155_out, not_156_out, not_157_out, not_158_out, not_159_out, not_160_out, not_161_out, not_162_out, F1, not_163_out);
  and and_23 (and_23_out, not_164_out, not_165_out, not_166_out, not_167_out, not_168_out, not_169_out, F5, not_170_out, not_171_out, not_172_out, not_173_out, not_174_out);
  and and_24 (and_24_out, not_175_out, not_176_out, not_177_out, not_178_out, not_179_out, not_180_out, F5, not_181_out, not_182_out, not_183_out, not_184_out, F0);
  and and_25 (and_25_out, not_185_out, not_186_out, not_187_out, not_188_out, not_189_out, not_190_out, F5, not_191_out, not_192_out, not_193_out, F1, not_194_out);
  and and_26 (and_26_out, not_195_out, not_196_out, not_197_out, not_198_out, not_199_out, not_200_out, F5, not_201_out, not_202_out, F2, not_203_out, not_204_out);
  and and_27 (and_27_out, not_205_out, not_206_out, not_207_out, not_208_out, not_209_out, not_210_out, F5, not_211_out, not_212_out, F2, not_213_out, F0);
  and and_28 (and_28_out, not_214_out, not_215_out, not_216_out, not_217_out, not_218_out, not_219_out, F5, not_220_out, not_221_out, F2, F1, F0);
  and and_29 (and_29_out, not_222_out, not_223_out, not_224_out, not_225_out, not_226_out, not_227_out, F5, not_228_out, F3, not_229_out, F1, not_230_out);
  and and_30 (and_30_out, not_231_out, not_232_out, not_233_out, not_234_out, not_235_out, not_236_out, F5, not_237_out, F3, not_238_out, F1, F0);
  and and_31 (and_31_out, not_239_out, not_240_out, not_241_out, not_242_out, not_243_out, not_244_out, not_245_out, not_246_out, F3, F2, not_247_out, not_248_out);
  and and_32 (and_32_out, not_249_out, not_250_out, not_251_out, OP2, not_252_out, not_253_out);
  and and_33 (and_33_out, not_254_out, not_255_out, not_256_out, OP2, not_257_out, OP0);
  and and_34 (and_34_out, OP5, not_258_out, OP3, not_259_out, OP1, OP0);
  or or_1 (R1_Used, and_1_out, and_2_out, and_3_out, and_4_out, and_5_out, and_6_out, and_7_out, and_8_out, and_9_out, and_10_out, and_11_out, and_12_out, and_13_out, and_14_out, and_15_out, and_16_out, and_17_out, and_18_out, and_19_out);
  or or_2 (R2_Used, and_20_out, and_21_out, and_22_out, and_23_out, and_24_out, and_25_out, and_26_out, and_27_out, and_28_out, and_29_out, and_30_out, and_31_out, and_32_out, and_33_out, and_34_out);
endmodule

module \数据相关检测  (
  input  R1_Used,
  input  [4:0] R1_num,
  input  EX_RegWrite,
  input  [4:0] EX_Write_num,
  input  [4:0] R2_num,
  input  R2_Used,
  input  MEM_RegWrite,
  input  [4:0] MEM_Write_num,
  output Relate_Out
);

  wire and_1_out, and_2_out, and_3_out, and_4_out, and_5_out, and_6_out, and_7_out, and_8_out,
       comparator_1_gt, comparator_2_gt, comparator_3_eq, comparator_4_eq, comparator_5_eq, comparator_6_eq,
       or_1_out, or_2_out;

  Comparator #(.width(5), .mode("unsigned")) comparator_1 (
    .a(R1_num), .b({5{1'b0}}), .gt(comparator_1_gt));  // open: eq, lt
  Comparator #(.width(5), .mode("unsigned")) comparator_2 (
    .a(R2_num), .b({5{1'b0}}), .gt(comparator_2_gt));  // open: eq, lt
  Comparator #(.width(5), .mode("unsigned")) comparator_3 (
    .a(R1_num), .b(MEM_Write_num), .eq(comparator_3_eq));  // open: gt, lt
  and and_1 (and_1_out, comparator_1_gt, R1_Used);
  and and_2 (and_2_out, and_1_out, comparator_4_eq);
  Comparator #(.width(5), .mode("unsigned")) comparator_4 (
    .a(R1_num), .b(EX_Write_num), .eq(comparator_4_eq));  // open: gt, lt
  and and_3 (and_3_out, and_4_out, comparator_5_eq);
  Comparator #(.width(5), .mode("unsigned")) comparator_5 (
    .a(R2_num), .b(EX_Write_num), .eq(comparator_5_eq));  // open: gt, lt
  and and_4 (and_4_out, R2_Used, comparator_2_gt);
  and and_5 (and_5_out, and_1_out, comparator_3_eq);
  and and_6 (and_6_out, and_4_out, comparator_6_eq);
  Comparator #(.width(5), .mode("unsigned")) comparator_6 (
    .a(R2_num), .b(MEM_Write_num), .eq(comparator_6_eq));  // open: gt, lt
  or or_1 (or_1_out, and_2_out, and_3_out);
  or or_2 (or_2_out, and_5_out, and_6_out);
  and and_7 (and_7_out, EX_RegWrite, or_1_out);
  and and_8 (and_8_out, MEM_RegWrite, or_2_out);
  or or_3 (Relate_Out, and_7_out, and_8_out);
endmodule

module \数据重定向检测  (
  input  EX_RegWrite,
  input  R1_Used,
  input  MEM_RegWrite,
  input  [4:0] R1_num,
  input  [4:0] EX_Write_num,
  input  [4:0] MEM_Write_num,
  input  [4:0] R2_num,
  input  R2_Used,
  output R1MEN,
  output R1WB,
  output R2MEN,
  output R2WB
);

  wire and_1_out, and_2_out, comparator_1_gt, comparator_2_eq, comparator_3_gt, comparator_4_eq,
       comparator_5_eq, comparator_6_eq;

  Comparator #(.width(5), .mode("unsigned")) comparator_1 (
    .a(R1_num), .b({5{1'b0}}), .gt(comparator_1_gt));  // open: eq, lt
  Comparator #(.width(5), .mode("twosComplement")) comparator_2 (
    .a(R1_num), .b(MEM_Write_num), .eq(comparator_2_eq));  // open: gt, lt
  Comparator #(.width(5), .mode("unsigned")) comparator_3 (
    .a(R2_num), .b({5{1'b0}}), .gt(comparator_3_gt));  // open: eq, lt
  and and_1 (and_1_out, comparator_1_gt, R1_Used);
  Comparator #(.width(5), .mode("twosComplement")) comparator_4 (
    .a(R1_num), .b(EX_Write_num), .eq(comparator_4_eq));  // open: gt, lt
  Comparator #(.width(5), .mode("twosComplement")) comparator_5 (
    .a(R2_num), .b(EX_Write_num), .eq(comparator_5_eq));  // open: gt, lt
  and and_2 (and_2_out, R2_Used, comparator_3_gt);
  Comparator #(.width(5), .mode("twosComplement")) comparator_6 (
    .a(R2_num), .b(MEM_Write_num), .eq(comparator_6_eq));  // open: gt, lt
  and and_3 (R1MEN, and_1_out, EX_RegWrite, comparator_4_eq);
  and and_4 (R1WB, and_1_out, MEM_RegWrite, comparator_2_eq);
  and and_5 (R2MEN, and_2_out, EX_RegWrite, comparator_5_eq);
  and and_6 (R2WB, and_2_out, MEM_RegWrite, comparator_6_eq);
endmodule

module \load_use检测  (
  input  R1_Used,
  input  EX_LW,
  input  [4:0] R1_num,
  input  [4:0] EX_Write_num,
  input  [4:0] R2_num,
  input  R2_Used,
  output stall
);

  wire and_1_out, and_2_out, and_3_out, and_4_out, comparator_1_eq, comparator_2_gt, comparator_3_eq,
       comparator_4_eq, or_1_out;

  Comparator #(.width(5), .mode("unsigned")) comparator_1 (
    .a(R1_num), .b({5{1'b0}}), .eq(comparator_1_eq));  // open: gt, lt
  Comparator #(.width(5), .mode("unsigned")) comparator_2 (
    .a(R2_num), .b({5{1'b0}}), .gt(comparator_2_gt));  // open: eq, lt
  and and_1 (and_1_out, R1_Used, comparator_1_eq);
  and and_2 (and_2_out, and_1_out, comparator_3_eq);
  Comparator #(.width(5), .mode("unsigned")) comparator_3 (
    .a(R1_num), .b(EX_Write_num), .eq(comparator_3_eq));  // open: gt, lt
  Comparator #(.width(5), .mode("unsigned")) comparator_4 (
    .a(EX_Write_num), .b(R2_num), .eq(comparator_4_eq));  // open: gt, lt
  and and_3 (and_3_out, comparator_4_eq, and_4_out);
  and and_4 (and_4_out, R2_Used, comparator_2_gt);
  or or_1 (or_1_out, and_2_out, and_3_out);
  and and_5 (stall, EX_LW, or_1_out);
endmodule
